// Logisim project 4位二进制数的格雷码表示.circ as structural Verilog: 1 circuit, main circuit main
module main (
  input  [3:0] in_1,
  output [3:0] out_2
);

  xor xor_1 (out_2[0], in_1[0], in_1[1]);
  xor xor_2 (out_2[1], in_1[1], in_1[2]);
  xor xor_3 (out_2[2], in_1[2], in_1[3]);

  assign out_2[3] = in_1[3];

  // Notes on the sheet:
  //   格雷码：最高位保留， 其余位与前一位异或
endmodule
