// Logisim project 多路选择器的实现方式.circ as structural Verilog: 1 circuit, main circuit main
module main (
  input  D0,
  input  D1,
  input  S,
  input  d0_2,
  input  d1_2,
  input  s_2,
  output out_7,
  output out_8
);

  wire and_1_out, and_2_out, nand_1_out, nand_2_out, not_1_out, not_2_out;

  not not_1 (not_1_out, S);
  not not_2 (not_2_out, s_2);
  and and_1 (and_1_out, D0, not_1_out);
  and and_2 (and_2_out, D1, S);
  nand nand_1 (nand_1_out, d0_2, not_2_out);
  nand nand_2 (nand_2_out, d1_2, s_2);
  or or_1 (out_7, and_1_out, and_2_out);
  nand nand_3 (out_8, nand_1_out, nand_2_out);
endmodule
