// Logisim project lab2.1.circ as structural Verilog: 1 circuit, main circuit main
module main (
  input  G1,
  input  G2A_L,
  input  G2B_L,
  input  A,
  input  B,
  input  C,
  output Y0_L,
  output Y1_L,
  output Y2_L,
  output Y3_L,
  output Y4_L,
  output Y5_L,
  output Y6_L,
  output Y7_L
);

  wire and_1_out, and_2_out, and_3_out, and_4_out, and_5_out, and_6_out, and_7_out, and_8_out, and_9_out,
       not_1_out, not_2_out, not_3_out, not_4_out, not_5_out, not_6_out, not_7_out, not_8_out, not_9_out,
       not_10_out, not_11_out, not_12_out, not_13_out, not_14_out;

  not not_1 (not_1_out, G2A_L);
  not not_2 (not_2_out, G2B_L);
  and and_1 (and_1_out, G1, not_1_out, not_2_out);
  not not_3 (not_3_out, C);
  not not_4 (not_4_out, B);
  not not_5 (not_5_out, A);
  not not_6 (not_6_out, C);
  not not_7 (not_7_out, B);
  not not_8 (not_8_out, C);
  not not_9 (not_9_out, A);
  not not_10 (not_10_out, C);
  not not_11 (not_11_out, B);
  not not_12 (not_12_out, A);
  not not_13 (not_13_out, B);
  not not_14 (not_14_out, A);
  not not_15 (Y0_L, and_2_out);
  and and_2 (and_2_out, and_1_out, not_3_out, not_4_out, not_5_out);
  and and_3 (and_3_out, and_1_out, not_6_out, not_7_out, A);
  not not_16 (Y1_L, and_3_out);
  and and_4 (and_4_out, and_1_out, not_8_out, B, not_9_out);
  not not_17 (Y2_L, and_4_out);
  not not_18 (Y3_L, and_5_out);
  and and_5 (and_5_out, and_1_out, not_10_out, B, A);
  and and_6 (and_6_out, and_1_out, C, not_11_out, not_12_out);
  not not_19 (Y4_L, and_6_out);
  and and_7 (and_7_out, and_1_out, C, not_13_out, A);
  not not_20 (Y5_L, and_7_out);
  not not_21 (Y6_L, and_8_out);
  and and_8 (and_8_out, and_1_out, C, B, not_14_out);
  not not_22 (Y7_L, and_9_out);
  and and_9 (and_9_out, and_1_out, C, B, A);

  // Notes on the sheet:
  //   输入引脚
  //   请勿修改引脚名称、电路名称及电路封装外观
  //   提示：使用独立逻辑门实现3-8译码器，禁止直接使用译码器组件。
  //   输出引脚
endmodule
