// Logisim project lab2.4.circ as structural Verilog: 3 circuits, main circuit main
module main (
  input  [6:0] Input,
  output [6:0] Output,
  output NoError
);

  wire \n3_8译码器_1_y1_l , \n3_8译码器_1_y2_l , \n3_8译码器_1_y3_l , \n3_8译码器_1_y4_l , \n3_8译码器_1_y5_l ,
       \n3_8译码器_1_y6_l , \n3_8译码器_1_y7_l , \n4位奇偶校验器_1_odd , \n4位奇偶校验器_2_odd , \n4位奇偶校验器_3_odd , not_1_out;

  \_4位奇偶校验器  \u_4位奇偶校验器_1  (
    .N0(Input[0]), .N1(Input[2]), .N2(Input[4]), .N3(Input[6]), .ODD(\n4位奇偶校验器_1_odd ));  // open: EVEN
  \_4位奇偶校验器  \u_4位奇偶校验器_2  (
    .N0(Input[1]), .N1(Input[2]), .N2(Input[5]), .N3(Input[6]), .ODD(\n4位奇偶校验器_2_odd ));  // open: EVEN
  \_4位奇偶校验器  \u_4位奇偶校验器_3  (
    .N0(Input[3]), .N1(Input[4]), .N2(Input[5]), .N3(Input[6]), .ODD(\n4位奇偶校验器_3_odd ));  // open: EVEN
  not not_1 (not_1_out, 1'b1);
  \_3_8译码器  \u_3_8译码器_1  (
    .G1(1'b1), .G2A_L(not_1_out), .G2B_L(not_1_out), .A(\n4位奇偶校验器_1_odd ), .B(\n4位奇偶校验器_2_odd ),
    .C(\n4位奇偶校验器_3_odd ), .Y0_L(NoError), .Y1_L(\n3_8译码器_1_y1_l ), .Y2_L(\n3_8译码器_1_y2_l ),
    .Y3_L(\n3_8译码器_1_y3_l ), .Y4_L(\n3_8译码器_1_y4_l ), .Y5_L(\n3_8译码器_1_y5_l ), .Y6_L(\n3_8译码器_1_y6_l ),
    .Y7_L(\n3_8译码器_1_y7_l ));
  xor xor_1 (Output[0], Input[0], \n3_8译码器_1_y1_l );
  xor xor_2 (Output[1], Input[1], \n3_8译码器_1_y2_l );
  xor xor_3 (Output[2], Input[2], \n3_8译码器_1_y3_l );
  xor xor_4 (Output[3], Input[3], \n3_8译码器_1_y4_l );
  xor xor_5 (Output[4], Input[4], \n3_8译码器_1_y5_l );
  xor xor_6 (Output[5], Input[5], \n3_8译码器_1_y6_l );
  xor xor_7 (Output[6], Input[6], \n3_8译码器_1_y7_l );
  Hex_Digit_Display hex_digit_display_1 ();  // open: value, dp

  // Notes on the sheet:
  //   输入引脚
  //   输入引脚
  //   请勿修改引脚名称、电路名称及电路封装外观
  //   提示：使用异或门、4位奇偶校验电路和74x138子电路实现7位汉明码纠错电路。
  //   输出引脚
endmodule

module \_3_8译码器  (
  input  G1,
  input  G2A_L,
  input  G2B_L,
  input  A,
  input  B,
  input  C,
  output Y0_L,
  output Y1_L,
  output Y2_L,
  output Y3_L,
  output Y4_L,
  output Y5_L,
  output Y6_L,
  output Y7_L
);

  wire and_1_out, not_1_out, not_2_out, not_3_out, not_4_out, not_5_out, not_6_out, not_7_out, not_8_out,
       not_9_out, not_10_out, not_11_out, not_12_out, not_13_out, not_14_out;

  not not_1 (not_1_out, G2A_L);
  not not_2 (not_2_out, G2B_L);
  and and_1 (and_1_out, G1, not_1_out, not_2_out);
  not not_3 (not_3_out, A);
  and and_2 (Y0_L, and_1_out, not_3_out, not_4_out, not_5_out);
  not not_4 (not_4_out, B);
  not not_5 (not_5_out, C);
  and and_3 (Y1_L, and_1_out, A, not_6_out, not_7_out);
  not not_6 (not_6_out, B);
  not not_7 (not_7_out, C);
  not not_8 (not_8_out, A);
  and and_4 (Y2_L, and_1_out, not_8_out, B, not_9_out);
  not not_9 (not_9_out, C);
  and and_5 (Y3_L, and_1_out, A, B, not_10_out);
  not not_10 (not_10_out, C);
  not not_11 (not_11_out, A);
  and and_6 (Y4_L, and_1_out, not_11_out, not_12_out, C);
  not not_12 (not_12_out, B);
  and and_7 (Y5_L, and_1_out, A, not_13_out, C);
  not not_13 (not_13_out, B);
  not not_14 (not_14_out, A);
  and and_8 (Y6_L, and_1_out, not_14_out, B, C);
  and and_9 (Y7_L, and_1_out, A, B, C);

  // Notes on the sheet:
  //   3-8译码器
endmodule

module \_4位奇偶校验器  (
  input  N0,
  input  N1,
  input  N2,
  input  N3,
  output EVEN,
  output ODD
);

  wire xor_1_out, xor_2_out;

  xor xor_1 (xor_1_out, N0, N1);
  xor xor_2 (xor_2_out, N2, N3);
  xnor xnor_1 (EVEN, xor_1_out, xor_2_out);
  not not_1 (ODD, EVEN);

  // Notes on the sheet:
  //   4位奇偶校验电路
endmodule
