// Logisim project lab3.2.circ as structural Verilog: 1 circuit, main circuit SHRG4U
module SHRG4U (
  input  CLK,
  input  CLR_L,
  input  RIN,
  input  D3,
  input  D2,
  input  D1,
  input  D0,
  input  LIN,
  input  S1,
  input  S0,
  output Q3,
  output Q2,
  output Q1,
  output Q0
);

  wire and_1_out, and_2_out, and_3_out, and_4_out, and_5_out, and_6_out, and_7_out, and_8_out, and_9_out,
       and_10_out, and_11_out, and_12_out, and_13_out, and_14_out, and_15_out, and_16_out, not_1_out,
       not_2_out, not_3_out, not_4_out, not_5_out, not_6_out, not_7_out, not_8_out, not_9_out, not_10_out,
       or_1_out, or_2_out, or_3_out, or_4_out, QA_qn, QB_qn, QC_qn, QD_qn;

  not not_1 (not_1_out, CLK);
  not not_2 (not_2_out, CLR_L);
  not not_3 (not_3_out, not_4_out);
  not not_4 (not_4_out, S1);
  not not_5 (not_5_out, S0);
  not not_6 (not_6_out, not_5_out);
  and and_1 (and_1_out, not_3_out, not_5_out, RIN);
  and and_2 (and_2_out, not_4_out, not_5_out, not_7_out);
  and and_3 (and_3_out, not_3_out, not_6_out, D3);
  and and_4 (and_4_out, not_4_out, not_6_out, not_8_out);
  and and_5 (and_5_out, not_3_out, not_5_out, not_7_out);
  and and_6 (and_6_out, not_4_out, not_5_out, not_8_out);
  and and_7 (and_7_out, not_3_out, not_6_out, D2);
  and and_8 (and_8_out, not_4_out, not_6_out, not_9_out);
  and and_9 (and_9_out, not_3_out, not_5_out, not_8_out);
  and and_10 (and_10_out, not_4_out, not_5_out, not_9_out);
  and and_11 (and_11_out, not_3_out, not_6_out, D1);
  and and_12 (and_12_out, not_4_out, not_6_out, not_10_out);
  and and_13 (and_13_out, not_3_out, not_5_out, not_9_out);
  and and_14 (and_14_out, not_4_out, not_5_out, not_10_out);
  and and_15 (and_15_out, not_3_out, not_6_out, D0);
  and and_16 (and_16_out, not_4_out, not_6_out, LIN);
  or or_1 (or_1_out, and_1_out, and_2_out, and_3_out, and_4_out);
  or or_2 (or_2_out, and_5_out, and_6_out, and_7_out, and_8_out);
  or or_3 (or_3_out, and_9_out, and_10_out, and_11_out, and_12_out);
  or or_4 (or_4_out, and_13_out, and_14_out, and_15_out, and_16_out);
  D_Flip_Flop #(.trigger("falling")) QD (
    .clk(not_1_out), .D(or_1_out), .Q(Q3), .Qn(QD_qn), .reset(not_2_out));  // open: preset
  not not_7 (not_7_out, QD_qn);
  D_Flip_Flop #(.trigger("falling")) QC (
    .clk(not_1_out), .D(or_2_out), .Q(Q2), .Qn(QC_qn), .reset(not_2_out));  // open: preset
  not not_8 (not_8_out, QC_qn);
  D_Flip_Flop #(.trigger("falling")) QB (
    .clk(not_1_out), .D(or_3_out), .Q(Q1), .Qn(QB_qn), .reset(not_2_out));  // open: preset
  not not_9 (not_9_out, QB_qn);
  D_Flip_Flop #(.trigger("falling")) QA (
    .clk(not_1_out), .D(or_4_out), .Q(Q0), .Qn(QA_qn), .reset(not_2_out));  // open: preset
  not not_10 (not_10_out, QA_qn);

  // Notes on the sheet:
  //   输入引脚
  //   请勿修改引脚名称、电路名称及电路封装外观
  //   提示：使用独立逻辑门实现4位异步清零移位寄存器，禁止直接使用移位寄存器组件。
  //   输出引脚
endmodule
