// Logisim project lab3.5.circ as structural Verilog: 1 circuit, main circuit main
module main (
  input  CLK,
  input  LD,
  input  [3:0] HH1,
  input  [3:0] HH0,
  input  [3:0] MM1,
  input  [3:0] MM0,
  input  [3:0] SS1,
  input  [3:0] SS0,
  output [3:0] HH_H,
  output [3:0] HH_L,
  output [3:0] MM_H,
  output [3:0] MM_L,
  output [3:0] SS_H,
  output [3:0] SS_L,
  output LED_R,
  output LED_G,
  output LED_B,
  output INErr
);

  wire and_1_out, and_2_out, and_5_out, and_6_out, and_9_out, and_11_out, and_14_out, and_15_out, and_16_out,
       and_17_out, and_19_out, cntr4u_1_p3, cntr4u_1_p14, cntr4u_2_p5, cntr4u_2_p6, cntr4u_2_p7,
       cntr4u_2_p10, cntr4u_2_p11, cntr4u_2_p13, cntr4u_3_p3, cntr4u_4_p3, cntr4u_5_p4, cntr4u_6_p3,
       cntr4u_7_p3, cntr4u_7_p14, comparator_1_eq, comparator_1_gt, comparator_2_gt, comparator_3_gt,
       comparator_4_gt, comparator_5_gt, comparator_6_gt, comparator_7_gt, LED_EN, not_1_out, not_2_out,
       not_3_out, not_7_out, not_8_out, not_9_out, not_10_out, not_12_out, not_13_out, not_14_out,
       not_15_out, not_16_out, not_17_out, not_18_out, not_19_out, not_20_out, not_21_out, not_22_out,
       not_23_out, not_24_out, not_26_out, or_1_out, START, STOP;

  not not_1 (not_1_out, INErr);
  and and_1 (and_1_out, LD, not_1_out);
  Comparator #(.width(4), .mode("unsigned")) comparator_1 (
    .a(HH1), .b(4'b0010), .gt(comparator_1_gt), .eq(comparator_1_eq));  // open: lt
  Comparator #(.width(4), .mode("unsigned")) comparator_2 (.a(HH0), .b(4'b0011), .gt(comparator_2_gt));  // open: eq, lt
  Comparator #(.width(4), .mode("unsigned")) comparator_3 (.a(HH0), .b(4'b1001), .gt(comparator_3_gt));  // open: eq, lt
  Comparator #(.width(4), .mode("unsigned")) comparator_4 (.a(MM1), .b(4'b0101), .gt(comparator_4_gt));  // open: eq, lt
  Comparator #(.width(4), .mode("unsigned")) comparator_5 (.a(MM0), .b(4'b1001), .gt(comparator_5_gt));  // open: eq, lt
  Comparator #(.width(4), .mode("unsigned")) comparator_6 (.a(SS1), .b(4'b0101), .gt(comparator_6_gt));  // open: eq, lt
  Comparator #(.width(4), .mode("unsigned")) comparator_7 (.a(SS0), .b(4'b1001), .gt(comparator_7_gt));  // open: eq, lt
  // CNTR4U cntr4u_1: pin names not known; wires that end beside it: CLK, and_1_out, cntr4u_1_p3, SS0[0], SS0[1], SS0[2], SS0[3], 1'b1, 1'b1, SS_L[0], SS_L[1], SS_L[2], SS_L[3], cntr4u_1_p14
  not not_2 (not_2_out, SS_L[1]);
  not not_3 (not_3_out, SS_L[2]);
  and and_2 (and_2_out, comparator_1_eq, comparator_2_gt);
  Hex_Digit_Display hex_digit_display_1 (.value(HH_H));  // open: dp
  and and_3 (cntr4u_1_p3, SS_L[0], not_2_out, not_3_out, SS_L[3]);
  // CNTR4U cntr4u_2: pin names not known; wires that end beside it: CLK, LED_EN, STOP, 1'b1, cntr4u_2_p5, cntr4u_2_p6, cntr4u_2_p7, START, START, cntr4u_2_p10, cntr4u_2_p11, LED_B, cntr4u_2_p13
  not not_4 (cntr4u_2_p5, 1'b1);
  not not_5 (cntr4u_2_p6, 1'b1);
  not not_6 (cntr4u_2_p7, 1'b1);
  Hex_Digit_Display hex_digit_display_2 (.value(MM_H));  // open: dp
  Hex_Digit_Display hex_digit_display_3 (.value(HH_L), .dp(1'b1));
  Hex_Digit_Display hex_digit_display_4 (.value(MM_L), .dp(1'b1));
  Hex_Digit_Display hex_digit_display_5 (.value(SS_H));  // open: dp
  // CNTR4U cntr4u_3: pin names not known; wires that end beside it: CLK, and_1_out, cntr4u_3_p3, SS1[0], SS1[1], SS1[2], cntr4u_1_p3, SS_H[0], SS_H[1], SS_H[2], SS_H[3]
  xor xor_1 (LED_R, cntr4u_2_p10, cntr4u_2_p11);
  xor xor_2 (LED_G, cntr4u_2_p11, LED_B);
  not not_7 (not_7_out, cntr4u_2_p10);
  and and_4 (STOP, not_7_out, cntr4u_2_p11, not_8_out, cntr4u_2_p13);
  not not_8 (not_8_out, LED_B);
  not not_9 (not_9_out, cntr4u_2_p10);
  not not_10 (not_10_out, cntr4u_2_p11);
  not not_11 (START, and_5_out);
  and and_5 (and_5_out, not_9_out, not_10_out, not_12_out, not_13_out);
  not not_12 (not_12_out, LED_B);
  not not_13 (not_13_out, cntr4u_2_p13);
  Hex_Digit_Display hex_digit_display_6 (.value(SS_L), .dp(1'b1));
  not not_14 (not_14_out, SS_H[1]);
  and and_6 (and_6_out, SS_H[0], not_14_out, SS_H[2], not_15_out);
  not not_15 (not_15_out, SS_H[3]);
  or or_1 (or_1_out, comparator_1_gt, and_2_out, comparator_3_gt, comparator_4_gt, comparator_5_gt, comparator_6_gt, comparator_7_gt);
  and and_7 (cntr4u_3_p3, and_6_out, cntr4u_1_p3);
  and and_8 (INErr, or_1_out, LD);
  // CNTR4U cntr4u_4: pin names not known; wires that end beside it: CLK, and_1_out, cntr4u_4_p3, MM0[0], MM0[2], MM0[3], cntr4u_3_p3, MM_L[0], MM_L[1], MM_L[2], MM_L[3]
  // RGBLed RGBLED: pin names not known; wires that end beside it: LED_R, LED_G, LED_B
  not not_16 (not_16_out, MM_L[1]);
  not not_17 (not_17_out, MM_L[2]);
  and and_9 (and_9_out, MM_L[0], not_16_out, not_17_out, MM_L[3]);
  and and_10 (cntr4u_4_p3, and_9_out, and_6_out, cntr4u_1_p3);
  // CNTR4U cntr4u_5: pin names not known; wires that end beside it: MM1[1], CLK, and_1_out, cntr4u_5_p4, MM1[0], MM1[1], MM1[2], MM1[3], cntr4u_4_p3, cntr4u_4_p3, MM_H[0], MM_H[1], MM_H[2], MM_H[3]
  not not_18 (not_18_out, MM_H[1]);
  not not_19 (not_19_out, MM_H[3]);
  and and_11 (and_11_out, MM_H[0], not_18_out, MM_H[2], not_19_out);
  and and_12 (cntr4u_5_p4, and_11_out, and_9_out, and_6_out, cntr4u_1_p3);
  and and_13 (LED_EN, and_11_out, and_9_out, and_6_out, cntr4u_1_p3);
  // CNTR4U cntr4u_6: pin names not known; wires that end beside it: CLK, and_1_out, cntr4u_6_p3, HH0[0], HH0[1], HH0[2], HH0[3], cntr4u_5_p4, cntr4u_5_p4, HH_L[0], HH_L[1], HH_L[2], HH_L[3]
  not not_20 (not_20_out, HH_L[1]);
  not not_21 (not_21_out, HH_L[2]);
  not not_22 (not_22_out, HH_L[2]);
  not not_23 (not_23_out, HH_L[3]);
  and and_14 (and_14_out, HH_L[0], not_20_out, not_21_out, HH_L[3]);
  and and_15 (and_15_out, and_14_out, and_11_out, and_9_out, and_6_out, cntr4u_1_p3);
  or or_2 (cntr4u_6_p3, and_15_out, cntr4u_7_p3);
  and and_16 (and_16_out, and_11_out, and_9_out, and_6_out, cntr4u_1_p3, and_17_out);
  and and_17 (and_17_out, HH_L[0], HH_L[1], not_22_out, not_23_out);
  // CNTR4U cntr4u_7: pin names not known; wires that end beside it: CLK, and_1_out, cntr4u_7_p3, HH1[0], HH1[1], HH1[2], HH1[3], and_15_out, and_15_out, HH_H[0], HH_H[1], HH_H[2], HH_H[3], cntr4u_7_p14, CLK, and_1_out
  not not_24 (not_24_out, HH_H[0]);
  not not_25 (cntr4u_7_p14, HH_H[2]);
  not not_26 (not_26_out, HH_H[3]);
  and and_18 (cntr4u_7_p3, and_19_out, and_16_out);
  and and_19 (and_19_out, not_24_out, HH_H[1], cntr4u_7_p14, not_26_out);

  // Other names for the same wires on the sheet: H0[3:0] = HH_L; H1[3:0] = HH_H; M0[3:0] = MM_L; M1[3:0] = MM_H;
  //   S0[3:0] = SS_L; S1[3:0] = SS_H

  // Notes on the sheet:
  //   设置初始时间BCD码
  //   输入信号
  //   请勿修改引脚名称、电路名称及电路封装外观
  //   数字时钟
  //   提示：使用4位二进制加法计数器子电路、比较器和独立逻辑门组件实现数字时钟。
  //   在载入有效时，检测设置数据错误
  //   生成三色LED显示信号，持续10个时钟周期
endmodule
