// Logisim project lab4.3.circ as structural Verilog: 1 circuit, main circuit Adder32
// 加法器
module Adder32 (
  input  Cin,
  input  [31:0] X,
  input  [31:0] Y,
  output CF,
  output Cout,
  output OF,
  output SF,
  output [31:0] S,
  output ZF
);

  wire and_1_out, and_2_out, and_3_out, main_2_c16, not_1_out, not_2_out, or_2_out, or_3_out;

  or or_1 (OF, and_1_out, and_2_out);
  and and_1 (and_1_out, S[31], not_1_out);
  not not_1 (not_1_out, or_3_out);
  not not_2 (not_2_out, S[31]);
  and and_2 (and_2_out, not_2_out, and_3_out);
  or or_2 (or_2_out, S[0], S[1], S[2], S[3], S[4], S[5], S[6], S[7], S[8], S[9], S[10], S[11], S[12], S[13], S[14], S[15], S[16], S[17], S[18], S[19], S[20], S[21], S[22], S[23], S[24], S[25], S[26], S[27], S[28], S[29], S[30], S[31]);
  not not_3 (ZF, or_2_out);
  xor xor_1 (CF, Cout, Cin);
  or or_3 (or_3_out, Y[31], X[31]);
  and and_3 (and_3_out, Y[31], X[31]);
  // Probe on X
  // Probe on Y
  // Probe on S
  lab4_2_main main_1 (.X(X[31:16]), .Y(Y[31:16]), .C0(main_2_c16), .S(S[31:16]), .C16(Cout));  // open: Pg, Gg
  lab4_2_main main_2 (.X(X[15:0]), .Y(Y[15:0]), .C0(Cin), .S(S[15:0]), .C16(main_2_c16));  // open: Pg, Gg

  assign SF = S[31];

  // Notes on the sheet:
  //   Cin: pull=down
  //   X: pull=down
  //   Y: pull=down
  //   输入引脚区
  //   输出引脚区
  //   请勿修改引脚名称、电路名称及电路封装外观
  //   提示：使用16位并行加法器子电路实现32位快速加法器
  //   功能说明:32位Adder  S=X+Y，Cout为最高位进位位，Cin为进位输入， S为和，溢出OF、进位CF、零ZF、符号SF。
  //   +
  //   =
  //   无符号加法
endmodule
