// Logisim project lab4.4.circ as structural Verilog: 1 circuit, main circuit main
// 移位器
module main (
  input  [4:0] shamt,
  input  L_R,
  input  A_L,
  input  [31:0] DataIn,
  output [31:0] DataOut
);

  wire multiplexer_9_out, multiplexer_15_out, multiplexer_25_out;
  wire [0:0] multiplexer_2_out;
  wire [3:0] bit_extender_1_out, multiplexer_13_out;
  wire [7:0] bit_extender_2_out, multiplexer_23_out;
  wire [15:0] bit_extender_3_out, multiplexer_41_out;
  wire [31:0] multiplexer_6_out, multiplexer_8_out, multiplexer_14_out, multiplexer_24_out;
  wire [31:28] multiplexer_3_out;
  wire [31:31] multiplexer_1_out;

  Multiplexer #(.enable("false")) multiplexer_1 (.in0(1'b0), .in1(DataIn[31]), .out(multiplexer_1_out[31]), .sel(A_L));
  Multiplexer #(.enable("false")) multiplexer_2 (.in0(1'b0), .in1(DataIn[31]), .out(multiplexer_2_out[0]), .sel(A_L));
  Multiplexer #(.select(2), .width(32), .enable("false")) multiplexer_3 (
    .in0(DataIn), .in1(DataIn), .in2({multiplexer_1_out[31], DataIn[31:1]}),
    .in3({DataIn[30:0], multiplexer_2_out[0]}), .out({multiplexer_3_out[29:28], multiplexer_6_out[31:2]}),
    .sel({shamt[0], L_R}));
  Multiplexer #(.enable("false")) multiplexer_4 (
    .in0(1'b0), .in1(multiplexer_3_out[28]), .out(multiplexer_3_out[31]), .sel(A_L));
  Multiplexer #(.enable("false")) multiplexer_5 (
    .in0(1'b0), .in1(multiplexer_3_out[29]), .out(multiplexer_3_out[30]), .sel(A_L));
  Multiplexer #(.enable("false")) multiplexer_6 (
    .in0(1'b0), .in1(multiplexer_3_out[28]), .out(multiplexer_6_out[0]), .sel(A_L));
  Multiplexer #(.enable("false")) multiplexer_7 (
    .in0(1'b0), .in1(multiplexer_3_out[29]), .out(multiplexer_6_out[1]), .sel(A_L));
  Multiplexer #(.select(2), .width(32), .enable("false")) multiplexer_8 (
    .in0({multiplexer_3_out[29:28], multiplexer_6_out[31:2]}),
    .in1({multiplexer_3_out[29:28], multiplexer_6_out[31:2]}),
    .in2({multiplexer_3_out, multiplexer_6_out[31:4]}), .in3(multiplexer_6_out), .out(multiplexer_8_out),
    .sel({shamt[1], L_R}));
  Multiplexer #(.enable("false")) multiplexer_9 (
    .in0(1'b0), .in1(multiplexer_8_out[31]), .out(multiplexer_9_out), .sel(A_L));
  Multiplexer #(.enable("false")) multiplexer_10 (
    .in0(1'b0), .in1(multiplexer_8_out[31]), .out(multiplexer_13_out[3]), .sel(A_L));
  Multiplexer #(.enable("false")) multiplexer_11 (
    .in0(1'b0), .in1(multiplexer_8_out[30]), .out(multiplexer_13_out[2]), .sel(A_L));
  Multiplexer #(.enable("false")) multiplexer_12 (
    .in0(1'b0), .in1(multiplexer_8_out[29]), .out(multiplexer_13_out[1]), .sel(A_L));
  Multiplexer #(.enable("false")) multiplexer_13 (
    .in0(1'b0), .in1(multiplexer_8_out[28]), .out(multiplexer_13_out[0]), .sel(A_L));
  assign bit_extender_1_out = {{3{multiplexer_9_out}}, multiplexer_9_out};  // Bit_Extender bit_extender_1
  Multiplexer #(.select(2), .width(32), .enable("false")) multiplexer_14 (
    .in0(multiplexer_8_out), .in1(multiplexer_8_out), .in2({bit_extender_1_out, multiplexer_8_out[31:4]}),
    .in3({multiplexer_8_out[27:0], multiplexer_13_out}), .out(multiplexer_14_out), .sel({shamt[2], L_R}));
  Multiplexer #(.enable("false")) multiplexer_15 (
    .in0(1'b0), .in1(multiplexer_14_out[31]), .out(multiplexer_15_out), .sel(A_L));
  Multiplexer #(.enable("false")) multiplexer_16 (
    .in0(1'b0), .in1(multiplexer_14_out[30]), .out(multiplexer_23_out[6]), .sel(A_L));
  Multiplexer #(.enable("false")) multiplexer_17 (
    .in0(1'b0), .in1(multiplexer_14_out[31]), .out(multiplexer_23_out[7]), .sel(A_L));
  Multiplexer #(.enable("false")) multiplexer_18 (
    .in0(1'b0), .in1(multiplexer_14_out[29]), .out(multiplexer_23_out[5]), .sel(A_L));
  Multiplexer #(.enable("false")) multiplexer_19 (
    .in0(1'b0), .in1(multiplexer_14_out[28]), .out(multiplexer_23_out[4]), .sel(A_L));
  Multiplexer #(.enable("false")) multiplexer_20 (
    .in0(1'b0), .in1(multiplexer_14_out[27]), .out(multiplexer_23_out[3]), .sel(A_L));
  Multiplexer #(.enable("false")) multiplexer_21 (
    .in0(1'b0), .in1(multiplexer_14_out[26]), .out(multiplexer_23_out[2]), .sel(A_L));
  Multiplexer #(.enable("false")) multiplexer_22 (
    .in0(1'b0), .in1(multiplexer_14_out[25]), .out(multiplexer_23_out[1]), .sel(A_L));
  Multiplexer #(.enable("false")) multiplexer_23 (
    .in0(1'b0), .in1(multiplexer_14_out[24]), .out(multiplexer_23_out[0]), .sel(A_L));
  assign bit_extender_2_out = {{7{multiplexer_15_out}}, multiplexer_15_out};  // Bit_Extender bit_extender_2
  Multiplexer #(.select(2), .width(32), .enable("false")) multiplexer_24 (
    .in0(multiplexer_14_out), .in1(multiplexer_14_out), .in2({bit_extender_2_out, multiplexer_14_out[31:8]}),
    .in3({multiplexer_14_out[23:0], multiplexer_23_out}), .out(multiplexer_24_out), .sel({shamt[3], L_R}));
  Multiplexer #(.enable("false")) multiplexer_25 (
    .in0(1'b0), .in1(multiplexer_24_out[31]), .out(multiplexer_25_out), .sel(A_L));
  Multiplexer #(.enable("false")) multiplexer_26 (
    .in0(1'b0), .in1(multiplexer_24_out[31]), .out(multiplexer_41_out[15]), .sel(A_L));
  Multiplexer #(.enable("false")) multiplexer_27 (
    .in0(1'b0), .in1(multiplexer_24_out[29]), .out(multiplexer_41_out[13]), .sel(A_L));
  Multiplexer #(.enable("false")) multiplexer_28 (
    .in0(1'b0), .in1(multiplexer_24_out[30]), .out(multiplexer_41_out[14]), .sel(A_L));
  Multiplexer #(.enable("false")) multiplexer_29 (
    .in0(1'b0), .in1(multiplexer_24_out[28]), .out(multiplexer_41_out[12]), .sel(A_L));
  Multiplexer #(.enable("false")) multiplexer_30 (
    .in0(1'b0), .in1(multiplexer_24_out[27]), .out(multiplexer_41_out[11]), .sel(A_L));
  Multiplexer #(.enable("false")) multiplexer_31 (
    .in0(1'b0), .in1(multiplexer_24_out[26]), .out(multiplexer_41_out[10]), .sel(A_L));
  Multiplexer #(.enable("false")) multiplexer_32 (
    .in0(1'b0), .in1(multiplexer_24_out[25]), .out(multiplexer_41_out[9]), .sel(A_L));
  Multiplexer #(.enable("false")) multiplexer_33 (
    .in0(1'b0), .in1(multiplexer_24_out[24]), .out(multiplexer_41_out[8]), .sel(A_L));
  Multiplexer #(.enable("false")) multiplexer_34 (
    .in0(1'b0), .in1(multiplexer_24_out[23]), .out(multiplexer_41_out[7]), .sel(A_L));
  Multiplexer #(.enable("false")) multiplexer_35 (
    .in0(1'b0), .in1(multiplexer_24_out[21]), .out(multiplexer_41_out[5]), .sel(A_L));
  Multiplexer #(.enable("false")) multiplexer_36 (
    .in0(1'b0), .in1(multiplexer_24_out[22]), .out(multiplexer_41_out[6]), .sel(A_L));
  Multiplexer #(.enable("false")) multiplexer_37 (
    .in0(1'b0), .in1(multiplexer_24_out[20]), .out(multiplexer_41_out[4]), .sel(A_L));
  Multiplexer #(.enable("false")) multiplexer_38 (
    .in0(1'b0), .in1(multiplexer_24_out[19]), .out(multiplexer_41_out[3]), .sel(A_L));
  Multiplexer #(.enable("false")) multiplexer_39 (
    .in0(1'b0), .in1(multiplexer_24_out[18]), .out(multiplexer_41_out[2]), .sel(A_L));
  Multiplexer #(.enable("false")) multiplexer_40 (
    .in0(1'b0), .in1(multiplexer_24_out[17]), .out(multiplexer_41_out[1]), .sel(A_L));
  Multiplexer #(.enable("false")) multiplexer_41 (
    .in0(1'b0), .in1(multiplexer_24_out[16]), .out(multiplexer_41_out[0]), .sel(A_L));
  assign bit_extender_3_out = {{15{multiplexer_25_out}}, multiplexer_25_out};  // Bit_Extender bit_extender_3
  Multiplexer #(.select(2), .width(32), .enable("false")) multiplexer_42 (
    .in0(multiplexer_24_out), .in1(multiplexer_24_out),
    .in2({bit_extender_3_out, multiplexer_24_out[31:16]}),
    .in3({multiplexer_24_out[15:0], multiplexer_41_out}), .out(DataOut), .sel({shamt[4], L_R}));

  // Other names for the same wires on the sheet: Din[31:0] = DataIn; Left_Right = L_R; Arth_Logic = A_L;
  //   Dout[31:0] = DataOut

  // Notes on the sheet:
  //   L/R,A/L: 00逻辑右移，01算术右移，10逻辑左移，11：循环左移
  //   输入引脚
  //   请勿修改引脚名称、电路名称及电路封装外观
  //   提示：使用多路选择器、逻辑门实现32位桶形移位器，禁止直接使用移位器组件。
  //   输出引脚
endmodule
