// Logisim project lab4.5.circ as structural Verilog: 2 circuits, main circuit ALU
module ALU (
  input  [3:0] ALUctr,
  input  [31:0] A,
  input  [31:0] B,
  output Zero,
  output [31:0] S
);

  wire adder32_1_cout, adder32_1_of, adder32_1_sf, aluctrl_1_alctr, aluctrl_1_lrctr, aluctrl_1_sigctr,
       aluctrl_1_subctr, multiplexer_1_out, xor_3_out, xor_4_out;
  wire [2:0] aluctrl_1_opctr;
  wire [31:0] adder32_1_s, and_1_out, bit_extender_1_out, bit_extender_2_out, main_1_dataout, or_1_out,
       xor_1_out, xor_2_out;

  assign bit_extender_1_out = {{31{aluctrl_1_subctr}}, aluctrl_1_subctr};  // Bit_Extender bit_extender_1
  assign xor_1_out = B ^ bit_extender_1_out;  // XOR_Gate xor_1, 32 bits wide
  assign and_1_out = A & B;  // AND_Gate and_1, 32 bits wide
  assign or_1_out = A | B;  // OR_Gate or_1, 32 bits wide
  assign xor_2_out = A ^ B;  // XOR_Gate xor_2, 32 bits wide
  lab4_4_main main_1 (
    .L_R(aluctrl_1_lrctr), .shamt(B[4:0]), .DataIn(A), .DataOut(main_1_dataout), .A_L(aluctrl_1_alctr));
  Adder32 adder32_1 (
    .Cin(aluctrl_1_subctr), .Cout(adder32_1_cout), .X(A), .Y(xor_1_out), .S(adder32_1_s), .OF(adder32_1_of),
    .ZF(Zero), .SF(adder32_1_sf));  // open: CF
  ALUctrl aluctrl_1 (
    .SUBctr(aluctrl_1_subctr), .LRctr(aluctrl_1_lrctr), .SIGctr(aluctrl_1_sigctr), .ALctr(aluctrl_1_alctr),
    .OPctr(aluctrl_1_opctr), .ALUctr(ALUctr));
  xor xor_3 (xor_3_out, aluctrl_1_subctr, adder32_1_cout);
  Multiplexer #(.enable("false")) multiplexer_1 (
    .in0(xor_3_out), .in1(xor_4_out), .out(multiplexer_1_out), .sel(aluctrl_1_sigctr));
  xor xor_4 (xor_4_out, adder32_1_of, adder32_1_sf);
  Multiplexer #(.select(3), .width(32), .enable("false")) multiplexer_2 (
    .in0(adder32_1_s), .in1(and_1_out), .in2(or_1_out), .in3(xor_2_out), .in4(main_1_dataout), .in5(B),
    .in6(bit_extender_2_out), .out(S), .sel(aluctrl_1_opctr));  // open: in7
  assign bit_extender_2_out = {{31{1'b0}}, multiplexer_1_out};  // Bit_Extender bit_extender_2
  // Probe on A
  // Probe on B
  // Probe on S

  // Other names for the same wires on the sheet: Result[31:0] = S

  // Notes on the sheet:
  //   B: pull=down
  //   ALUctr: pull=down
  //   A: pull=down
  //   输入引脚
  //   请勿修改引脚名称、电路名称及电路封装外观
  //   提示：使用32位并行加法器子电路、桶形移位器、ALU控制子电路实现32位ALU
  //   功能说明:32位ALU，输入32位操作数A、B，4位控制信号ALUctr，输出32位结果Reseult和1位Zero标志位
  //   输出引脚
  //   操作数和结果
endmodule

module ALUctrl (
  input  [3:0] ALUctr,
  output SUBctr,
  output LRctr,
  output SIGctr,
  output ALctr,
  output [2:0] OPctr
);

  wire and_1_out, and_2_out, and_3_out, and_4_out, and_5_out, and_6_out, and_7_out, and_8_out, and_9_out,
       and_10_out, and_11_out, and_12_out, and_13_out, and_14_out, and_15_out, and_16_out, not_1_out,
       not_2_out, not_3_out, not_4_out;

  not not_1 (not_1_out, ALUctr[3]);
  not not_2 (not_2_out, ALUctr[2]);
  not not_3 (not_3_out, ALUctr[1]);
  not not_4 (not_4_out, ALUctr[0]);
  and and_1 (and_1_out, not_4_out, ALUctr[1], not_2_out, not_1_out);
  and and_2 (and_2_out, ALUctr[0], ALUctr[1], not_2_out, not_1_out);
  and and_3 (and_3_out, not_4_out, not_3_out, not_2_out, ALUctr[3]);
  and and_4 (and_4_out, ALUctr[0], not_3_out, not_2_out, not_1_out);
  and and_5 (and_5_out, not_4_out, ALUctr[1], not_2_out, not_1_out);
  and and_6 (and_6_out, ALUctr[0], ALUctr[1], not_2_out, not_1_out);
  and and_7 (and_7_out, ALUctr[0], not_3_out, ALUctr[2], not_1_out);
  and and_8 (and_8_out, ALUctr[0], not_3_out, ALUctr[2], ALUctr[3]);
  and and_9 (and_9_out, ALUctr[0], ALUctr[1], ALUctr[2], ALUctr[3]);
  and and_10 (and_10_out, not_4_out, ALUctr[1], not_2_out, not_1_out);
  and and_11 (and_11_out, ALUctr[0], ALUctr[1], not_2_out, not_1_out);
  and and_12 (and_12_out, not_4_out, not_3_out, ALUctr[2], not_1_out);
  and and_13 (and_13_out, not_4_out, ALUctr[1], ALUctr[2], not_1_out);
  and and_14 (and_14_out, not_4_out, not_3_out, ALUctr[2], not_1_out);
  and and_15 (and_15_out, ALUctr[0], ALUctr[1], ALUctr[2], not_1_out);
  and and_16 (and_16_out, ALUctr[0], ALUctr[1], ALUctr[2], ALUctr[3]);
  or or_1 (SUBctr, and_1_out, and_2_out, and_3_out);
  and and_17 (SIGctr, not_4_out, ALUctr[1], not_2_out, not_1_out);
  and and_18 (ALctr, ALUctr[0], not_3_out, ALUctr[2], ALUctr[3]);
  and and_19 (LRctr, ALUctr[0], not_3_out, not_2_out, not_1_out);
  or or_2 (OPctr[2], and_4_out, and_5_out, and_6_out, and_7_out, and_8_out, and_9_out);
  or or_3 (OPctr[1], and_10_out, and_11_out, and_12_out, and_13_out);
  or or_4 (OPctr[0], and_14_out, and_15_out, and_16_out);

  // Notes on the sheet:
  //   输入引脚
  //   ALU操作控制信号生成部件
  //   输出引脚
endmodule
