// Logisim project 32位无符号乘法器.circ as structural Verilog: 3 circuits, main circuit main
module main (
  input  [31:0] in_1,
  input  [31:0] in_2,
  input  in_3,
  input  in_4,
  output [31:0] out_5,
  output [31:0] out_6
);

  wire adder32_1_cout, Load, not_1_out, Stop;
  wire [7:0] \n32位计数器_1_q0 ;
  wire [31:0] adder32_1_s, multiplexer_1_out, multiplexer_2_out, \n64位逻辑右移移位器_1_out_4 , \n64位逻辑右移移位器_1_out_5 ;

  Hex_Digit_Display hex_digit_display_1 (.value(in_1[31:28]));  // open: dp
  Hex_Digit_Display hex_digit_display_2 (.value(in_2[31:28]));  // open: dp
  Hex_Digit_Display hex_digit_display_3 (.value(out_5[31:28]));  // open: dp
  Hex_Digit_Display hex_digit_display_4 (.value(out_6[31:28]));  // open: dp
  Hex_Digit_Display hex_digit_display_5 (.value(in_1[27:24]));  // open: dp
  Hex_Digit_Display hex_digit_display_6 (.value(in_2[27:24]));  // open: dp
  Hex_Digit_Display hex_digit_display_7 (.value(out_5[27:24]));  // open: dp
  Hex_Digit_Display hex_digit_display_8 (.value(out_6[27:24]));  // open: dp
  Hex_Digit_Display hex_digit_display_9 (.value(in_1[23:20]));  // open: dp
  Hex_Digit_Display hex_digit_display_10 (.value(in_1[19:16]));  // open: dp
  Hex_Digit_Display hex_digit_display_11 (.value(in_2[19:16]));  // open: dp
  Hex_Digit_Display hex_digit_display_12 (.value(in_2[23:20]));  // open: dp
  Hex_Digit_Display hex_digit_display_13 (.value(out_5[19:16]));  // open: dp
  Hex_Digit_Display hex_digit_display_14 (.value(out_5[23:20]));  // open: dp
  Hex_Digit_Display hex_digit_display_15 (.value(out_6[23:20]));  // open: dp
  Hex_Digit_Display hex_digit_display_16 (.value(out_6[19:16]));  // open: dp
  Hex_Digit_Display hex_digit_display_17 (.value(in_1[15:12]));  // open: dp
  Hex_Digit_Display hex_digit_display_18 (.value(in_2[15:12]));  // open: dp
  Hex_Digit_Display hex_digit_display_19 (.value(out_5[15:12]));  // open: dp
  Hex_Digit_Display hex_digit_display_20 (.value(out_6[15:12]));  // open: dp
  Hex_Digit_Display hex_digit_display_21 (.value(in_1[7:4]));  // open: dp
  Hex_Digit_Display hex_digit_display_22 (.value(in_1[11:8]));  // open: dp
  Hex_Digit_Display hex_digit_display_23 (.value(in_2[7:4]));  // open: dp
  Hex_Digit_Display hex_digit_display_24 (.value(in_2[11:8]));  // open: dp
  Hex_Digit_Display hex_digit_display_25 (.value(out_5[11:8]));  // open: dp
  Hex_Digit_Display hex_digit_display_26 (.value(out_5[7:4]));  // open: dp
  Hex_Digit_Display hex_digit_display_27 (.value(out_6[11:8]));  // open: dp
  Hex_Digit_Display hex_digit_display_28 (.value(out_6[7:4]));  // open: dp
  Hex_Digit_Display hex_digit_display_29 (.value(in_1[3:0]));  // open: dp
  Hex_Digit_Display hex_digit_display_30 (.value(in_2[3:0]));  // open: dp
  Hex_Digit_Display hex_digit_display_31 (.value(out_5[3:0]));  // open: dp
  Hex_Digit_Display hex_digit_display_32 (.value(out_6[3:0]));  // open: dp
  not not_1 (not_1_out, Stop);
  Register #(.width(32), .Select("low")) register_1 (
    .D(\n64位逻辑右移移位器_1_out_5 ), .en(not_1_out), .Q(out_6), .clk(in_3), .clr(in_4));
  Multiplexer #(.width(32), .enable("false")) multiplexer_1 (
    .in0({32{1'b0}}), .in1(in_1), .out(multiplexer_1_out), .sel(out_5[0]));
  Adder32 adder32_1 (
    .Cout(adder32_1_cout), .X(out_6), .Y(multiplexer_1_out), .S(adder32_1_s));  // open: Cin, OF, CF, ZF, SF
  Multiplexer #(.width(32), .enable("false")) multiplexer_2 (
    .in0(\n64位逻辑右移移位器_1_out_4 ), .in1(in_2), .out(multiplexer_2_out), .sel(Load));
  \_64位逻辑右移移位器  \u_64位逻辑右移移位器_1  (
    .in_2(out_5), .in_3(adder32_1_s), .out_4(\n64位逻辑右移移位器_1_out_4 ), .out_5(\n64位逻辑右移移位器_1_out_5 ),
    .in_1(adder32_1_cout));
  Register #(.width(32), .Select("low")) register_2 (
    .D(multiplexer_2_out), .en(not_1_out), .Q(out_5), .clk(in_3), .clr(in_4));
  \_32位计数器  \u_32位计数器_1  (
    .CLK(in_3), .LD(1'b0), .CLR(in_4), .Q0(\n32位计数器_1_q0 [0]), .Q1(\n32位计数器_1_q0 [1]),
    .Q2(\n32位计数器_1_q0 [2]), .Q3(\n32位计数器_1_q0 [3]), .ENP(not_1_out), .ENT(not_1_out), .Q4(\n32位计数器_1_q0 [4]),
    .Q5(\n32位计数器_1_q0 [5]), .Q6(\n32位计数器_1_q0 [6]), .Q7(\n32位计数器_1_q0 [7]));  // open: D0, D1, D2, D3, D4, D5, D6, D7, RCO
  Comparator comparator_1 (.a(\n32位计数器_1_q0 ), .b({8{1'b0}}), .eq(Load));  // open: gt, lt
  Comparator comparator_2 (.a(\n32位计数器_1_q0 ), .b(8'h21), .eq(Stop));  // open: gt, lt

  // Other names for the same wires on the sheet: CLK = in_3; RST = in_4; x[31:0] = in_1; y[31:0] = in_2;
  //   z_high32[31:0] = out_6; z_low32[31:0] = out_5
endmodule

module \_32位计数器  (
  input  CLK,
  input  LD,
  input  CLR,
  input  D0,
  input  D1,
  input  D2,
  input  D3,
  input  ENP,
  input  ENT,
  input  D4,
  input  D5,
  input  D6,
  input  D7,
  output Q0,
  output Q1,
  output Q2,
  output Q3,
  output Q4,
  output Q5,
  output Q6,
  output Q7,
  output RCO
);

  wire cntr4u_1_rco, register_1_q;

  CNTR4U cntr4u_1 (
    .CLK(CLK), .LD(LD), .CLR(CLR), .Q0(Q0), .Q1(Q1), .D0(D0), .D1(D1), .D2(D2), .Q2(Q2), .Q3(Q3), .D3(D3),
    .ENP(ENP), .ENT(ENT), .RCO(cntr4u_1_rco));
  Register #(.width(1), .Select("low")) register_1 (
    .D(cntr4u_1_rco), .en(1'b1), .Q(register_1_q), .clk(CLK));  // open: clr
  CNTR4U cntr4u_2 (
    .CLK(register_1_q), .LD(LD), .CLR(CLR), .Q0(Q4), .Q1(Q5), .D0(D4), .D1(D5), .D2(D6), .Q2(Q6), .Q3(Q7),
    .D3(D7), .ENP(ENP), .ENT(ENT), .RCO(RCO));

  // Notes on the sheet:
  //   输入引脚
  //   输出引脚
endmodule

module \_64位逻辑右移移位器  (
  input  in_1,
  input  [31:0] in_2,
  input  [31:0] in_3,
  output [31:0] out_4,
  output [31:0] out_5
);

  wire [0:0] not_1_out, not_2_out;
  wire [15:15] main_2_dataout;
  wire [31:31] main_1_dataout;

  not not_1 (not_1_out[0], 1'b0);
  lab4_4_main main_1 (
    .L_R(1'b0), .shamt({4'b0000, not_1_out[0]}), .DataIn(in_3), .DataOut({main_1_dataout[31], out_5[30:0]}),
    .A_L(1'b0));
  not not_2 (not_2_out[0], 1'b0);
  lab4_4_main main_2 (
    .L_R(1'b0), .shamt({4'b0000, not_2_out[0]}), .DataIn(in_2), .DataOut({main_2_dataout[15], out_4[30:0]}),
    .A_L(1'b0));

  assign out_4[31] = in_3[0];
  assign out_5[31] = in_1;

  // Other names for the same wires on the sheet: Din_high32[31:0] = in_3; Din_low32[31:0] = in_2;
  //   r_high32[31:0] = {in_1, out_5[30:0]}; Cin = in_1; r_low32[31:0] = {in_3[0], out_4[30:0]}
endmodule
