// Logisim project 64 位二进制快速加法器.circ as structural Verilog: 1 circuit, main circuit main
module main (
  input  [15:0] in_1,
  input  [15:0] in_2,
  input  [15:0] in_3,
  input  [15:0] in_4,
  input  Cin,
  input  [15:0] in_6,
  input  [15:0] in_7,
  input  [15:0] in_8,
  input  [15:0] in_9,
  output CF,
  output Cout,
  output OF,
  output SF,
  output ZF,
  output [15:0] out_15,
  output [15:0] out_16,
  output [15:0] out_17,
  output [15:0] out_18
);

  wire and_1_out, and_2_out, clu4_1_c1, clu4_1_c2, clu4_1_c3, main_1_gg, main_1_pg, main_2_gg, main_2_pg,
       main_3_gg, main_3_pg, main_4_gg, main_4_pg, not_1_out, not_2_out, not_3_out, or_1_out, or_2_out,
       or_4_out, or_5_out, or_6_out;

  lab4_2_main main_1 (.X(in_4), .Y(in_9), .C0(clu4_1_c3), .S(out_18), .Pg(main_1_pg), .Gg(main_1_gg));  // open: C16
  or or_1 (or_1_out, out_15[0], out_15[1], out_15[2], out_15[3], out_15[4], out_15[5], out_15[6], out_15[7], out_15[8], out_15[9], out_15[10], out_15[11], out_15[12], out_15[13], out_15[14], out_15[15]);
  not not_1 (not_1_out, out_18[15]);
  not not_2 (not_2_out, in_9[15]);
  not not_3 (not_3_out, in_4[15]);
  lab4_2_main main_2 (.X(in_3), .Y(in_8), .C0(clu4_1_c2), .S(out_17), .Pg(main_2_pg), .Gg(main_2_gg));  // open: C16
  and and_1 (and_1_out, in_9[15], not_1_out, in_4[15]);
  and and_2 (and_2_out, not_2_out, out_18[15], not_3_out);
  or or_2 (or_2_out, out_16[0], out_16[1], out_16[2], out_16[3], out_16[4], out_16[5], out_16[6], out_16[7], out_16[8], out_16[9], out_16[10], out_16[11], out_16[12], out_16[13], out_16[14], out_16[15]);
  CLU4 clu4_1 (
    .P0(main_4_pg), .P1(main_3_pg), .P2(main_2_pg), .P3(main_1_pg), .C1(clu4_1_c1), .C3(clu4_1_c3),
    .G0(main_4_gg), .G1(main_3_gg), .G2(main_2_gg), .G3(main_1_gg), .C2(clu4_1_c2), .C4(Cout), .C0(Cin));  // open: Pg, Gg
  lab4_2_main main_3 (.X(in_2), .Y(in_7), .C0(clu4_1_c1), .S(out_16), .Pg(main_3_pg), .Gg(main_3_gg));  // open: C16
  or or_3 (OF, and_1_out, and_2_out);
  or or_4 (or_4_out, out_17[0], out_17[1], out_17[2], out_17[3], out_17[4], out_17[5], out_17[6], out_17[7], out_17[8], out_17[9], out_17[10], out_17[11], out_17[12], out_17[13], out_17[14], out_17[15]);
  lab4_2_main main_4 (.X(in_1), .Y(in_6), .C0(Cin), .S(out_15), .Pg(main_4_pg), .Gg(main_4_gg));  // open: C16
  or or_5 (or_5_out, out_18[0], out_18[1], out_18[2], out_18[3], out_18[4], out_18[5], out_18[6], out_18[7], out_18[8], out_18[9], out_18[10], out_18[11], out_18[12], out_18[13], out_18[14], out_18[15]);
  xor xor_1 (CF, Cout, Cin);
  or or_6 (or_6_out, or_5_out, or_4_out, or_2_out, or_1_out);
  not not_4 (ZF, or_6_out);

  assign SF = out_18[15];

  // Other names for the same wires on the sheet: r0[15:0] = out_15; r1[15:0] = out_16; r2[15:0] = out_17;
  //   r3[15:0] = out_18; x0[15:0] = in_1; x1[15:0] = in_2; x2[15:0] = in_3; x3[15:0] = in_4; y0[15:0] = in_6;
  //   y1[15:0] = in_7; y2[15:0] = in_8; y3[15:0] = in_9

  // Notes on the sheet:
  //   Cin: pull=down
endmodule
