// Logisim project 滚动显示NJUCS.circ as structural Verilog: 1 circuit, main circuit main
module main (
);

  wire clock_1_out, cntr4u_1_p3, not_1_out;
  wire [2:0] cntr4u_1_p10;
  wire [6:0] multiplexer_1_out, multiplexer_2_out, multiplexer_3_out;
  wire [7:0] main_1_row1, main_1_row2, main_1_row3, main_1_row4, main_1_row5, main_1_row6, main_1_row7,
       main_1_row8, main_1_row9, main_1_row10, main_1_row11, main_1_row12, main_1_row13, main_1_row14,
       main_1_row15, main_1_row16, main_2_row1, main_2_row2, main_2_row3, main_2_row4, main_2_row5,
       main_2_row6, main_2_row7, main_2_row8, main_2_row9, main_2_row10, main_2_row11, main_2_row12,
       main_2_row13, main_2_row14, main_2_row15, main_2_row16, main_3_row1, main_3_row2, main_3_row3,
       main_3_row4, main_3_row5, main_3_row6, main_3_row7, main_3_row8, main_3_row9, main_3_row10,
       main_3_row11, main_3_row12, main_3_row13, main_3_row14, main_3_row15, main_3_row16;

  Clock clock_1 (.out(clock_1_out));
  not not_1 (not_1_out, 1'b0);
  // CNTR4U cntr4u_1: pin names not known; wires that end beside it: clock_1_out, 1'b0, cntr4u_1_p3, 1'b0, 1'b0, 1'b0, 1'b0, not_1_out, not_1_out, cntr4u_1_p10[0], cntr4u_1_p10[1], cntr4u_1_p10[2]
  Multiplexer #(.select(3), .width(7), .enable("false")) multiplexer_1 (
    .in0(7'b1001110), .in1(7'b1001010), .in2(7'b1010101), .in3(7'b1000011), .in4(7'b1010011),
    .out(multiplexer_1_out), .sel(cntr4u_1_p10));  // open: in5, in6, in7
  Comparator #(.width(3)) comparator_1 (.a(cntr4u_1_p10), .b(3'b100), .eq(cntr4u_1_p3));  // open: gt, lt
  DotMatrix #(.inputtype("row"), .matrixcols(8), .matrixrows(16)) dotmatrix_1 (
    .row0(main_1_row1), .row1(main_1_row2), .row2(main_1_row3), .row3(main_1_row4), .row4(main_1_row5),
    .row5(main_1_row6), .row6(main_1_row7), .row7(main_1_row8), .row8(main_1_row9), .row9(main_1_row10),
    .row10(main_1_row11), .row11(main_1_row12), .row12(main_1_row13), .row13(main_1_row14),
    .row14(main_1_row15), .row15(main_1_row16));
  lab5_1_main main_1 (
    .ASCII_CODE(multiplexer_1_out), .row1(main_1_row1), .row2(main_1_row2), .row3(main_1_row3),
    .row4(main_1_row4), .row7(main_1_row7), .row5(main_1_row5), .row6(main_1_row6), .row8(main_1_row8),
    .row9(main_1_row9), .row10(main_1_row10), .row11(main_1_row11), .row12(main_1_row12),
    .row13(main_1_row13), .row14(main_1_row14), .row15(main_1_row15), .row16(main_1_row16));  // open: CodeErr
  Multiplexer #(.select(3), .width(7), .enable("false")) multiplexer_2 (
    .in0(7'b1001010), .in1(7'b1010101), .in2(7'b1000011), .in3(7'b1010011), .in4(7'b1001110),
    .out(multiplexer_2_out), .sel(cntr4u_1_p10));  // open: in5, in6, in7
  lab5_1_main main_2 (
    .ASCII_CODE(multiplexer_2_out), .row1(main_2_row1), .row2(main_2_row2), .row3(main_2_row3),
    .row4(main_2_row4), .row7(main_2_row7), .row5(main_2_row5), .row6(main_2_row6), .row8(main_2_row8),
    .row9(main_2_row9), .row10(main_2_row10), .row11(main_2_row11), .row12(main_2_row12),
    .row13(main_2_row13), .row14(main_2_row14), .row15(main_2_row15), .row16(main_2_row16));  // open: CodeErr
  DotMatrix #(.inputtype("row"), .matrixcols(8), .matrixrows(16)) dotmatrix_2 (
    .row0(main_2_row1), .row1(main_2_row2), .row2(main_2_row3), .row3(main_2_row4), .row4(main_2_row5),
    .row5(main_2_row6), .row6(main_2_row7), .row7(main_2_row8), .row8(main_2_row9), .row9(main_2_row10),
    .row10(main_2_row11), .row11(main_2_row12), .row12(main_2_row13), .row13(main_2_row14),
    .row14(main_2_row15), .row15(main_2_row16));
  Multiplexer #(.select(3), .width(7), .enable("false")) multiplexer_3 (
    .in0(7'b1010101), .in1(7'b1000011), .in2(7'b1010011), .in3(7'b1001110), .in4(7'b1001010),
    .out(multiplexer_3_out), .sel(cntr4u_1_p10));  // open: in5, in6, in7
  DotMatrix #(.inputtype("row"), .matrixcols(8), .matrixrows(16)) dotmatrix_3 (
    .row0(main_3_row1), .row1(main_3_row2), .row2(main_3_row3), .row3(main_3_row4), .row4(main_3_row5),
    .row5(main_3_row6), .row6(main_3_row7), .row7(main_3_row8), .row8(main_3_row9), .row9(main_3_row10),
    .row10(main_3_row11), .row11(main_3_row12), .row12(main_3_row13), .row13(main_3_row14),
    .row14(main_3_row15), .row15(main_3_row16));
  lab5_1_main main_3 (
    .ASCII_CODE(multiplexer_3_out), .row1(main_3_row1), .row2(main_3_row2), .row3(main_3_row3),
    .row4(main_3_row4), .row7(main_3_row7), .row5(main_3_row5), .row6(main_3_row6), .row8(main_3_row8),
    .row9(main_3_row9), .row10(main_3_row10), .row11(main_3_row11), .row12(main_3_row12),
    .row13(main_3_row13), .row14(main_3_row14), .row15(main_3_row15), .row16(main_3_row16));  // open: CodeErr
endmodule
