// Logisim project lab6.1.circ as structural Verilog: 1 circuit, main circuit 控制器
module \控制器  (
  input  [6:0] opcode,
  input  [2:0] funct3,
  input  [6:0] funct7,
  output [2:0] ExtOp,
  output RegWr,
  output [2:0] BandJ,
  output ALUASrc,
  output [1:0] ALUBSrc,
  output [3:0] ALUctr,
  output MemtoReg,
  output [2:0] MemOp,
  output MemWr
);

  wire and_1_out, and_2_out, and_3_out, and_4_out, and_5_out, and_6_out, and_7_out, and_8_out, and_9_out,
       comparator_1_eq, comparator_2_eq, comparator_3_eq, comparator_4_eq, comparator_6_eq, comparator_7_eq,
       comparator_8_eq, comparator_9_eq, comparator_10_eq, comparator_11_eq, comparator_12_eq,
       comparator_13_eq, comparator_14_eq, comparator_15_eq, comparator_18_eq, comparator_19_eq,
       comparator_20_eq, comparator_21_eq, comparator_22_eq, comparator_23_eq, comparator_24_eq,
       comparator_25_eq, comparator_25_lt, comparator_26_eq, comparator_27_eq, comparator_28_eq,
       comparator_29_eq, comparator_30_eq, comparator_31_eq, comparator_32_eq, comparator_33_eq, not_1_out,
       not_2_out, or_7_out, or_8_out;

  Comparator #(.width(7)) comparator_1 (.a(opcode), .b(7'b0110111), .eq(comparator_1_eq));  // open: gt, lt
  Comparator #(.width(7)) comparator_2 (.a(opcode), .b(7'b0010111), .eq(comparator_2_eq));  // open: gt, lt
  Comparator #(.width(7)) comparator_3 (.a(opcode), .b(7'b1100011), .eq(comparator_3_eq));  // open: gt, lt
  Comparator #(.width(7)) comparator_4 (.a(opcode), .b(7'b0100011), .eq(comparator_4_eq));  // open: gt, lt
  Comparator #(.width(7)) comparator_5 (.a(opcode), .b(7'b1101111), .eq(ExtOp[2]));  // open: gt, lt
  Comparator #(.width(7)) comparator_6 (.a(opcode), .b(7'b0010111), .eq(comparator_6_eq));  // open: gt, lt
  Comparator #(.width(7)) comparator_7 (.a(opcode), .b(7'b1101111), .eq(comparator_7_eq));  // open: gt, lt
  Comparator #(.width(7)) comparator_8 (.a(opcode), .b(7'b1100111), .eq(comparator_8_eq));  // open: gt, lt
  Comparator #(.width(7)) comparator_9 (.a(opcode), .b(7'b0110111), .eq(comparator_9_eq));  // open: gt, lt
  Comparator #(.width(7)) comparator_10 (.a(opcode), .b(7'b0010111), .eq(comparator_10_eq));  // open: gt, lt
  Comparator #(.width(7)) comparator_11 (.a(opcode), .b(7'b0010011), .eq(comparator_11_eq));  // open: gt, lt
  Comparator #(.width(7)) comparator_12 (.a(opcode), .b(7'b0000011), .eq(comparator_12_eq));  // open: gt, lt
  Comparator #(.width(7)) comparator_13 (.a(opcode), .b(7'b0100011), .eq(comparator_13_eq));  // open: gt, lt
  Comparator #(.width(7)) comparator_14 (.a(opcode), .b(7'b1101111), .eq(comparator_14_eq));  // open: gt, lt
  Comparator #(.width(7)) comparator_15 (.a(opcode), .b(7'b1100111), .eq(comparator_15_eq));  // open: gt, lt
  Comparator #(.width(7)) comparator_16 (.a(opcode), .b(7'b0000011), .eq(MemtoReg));  // open: gt, lt
  Comparator #(.width(7)) comparator_17 (.a(opcode), .b(7'b0100011), .eq(MemWr));  // open: gt, lt
  Comparator #(.width(7)) comparator_18 (.a(opcode), .b(7'b0000011), .eq(comparator_18_eq));  // open: gt, lt
  Comparator #(.width(7)) comparator_19 (.a(opcode), .b(7'b1100111), .eq(comparator_19_eq));  // open: gt, lt
  Comparator #(.width(7)) comparator_20 (.a(opcode), .b(7'b1101111), .eq(comparator_20_eq));  // open: gt, lt
  Comparator #(.width(7)) comparator_21 (.a(opcode), .b(7'b0110011), .eq(comparator_21_eq));  // open: gt, lt
  Comparator #(.width(7)) comparator_22 (.a(opcode), .b(7'b0010011), .eq(comparator_22_eq));  // open: gt, lt
  Comparator #(.width(7)) comparator_23 (.a(opcode), .b(7'b0010111), .eq(comparator_23_eq));  // open: gt, lt
  Comparator #(.width(7)) comparator_24 (.a(opcode), .b(7'b0110111), .eq(comparator_24_eq));  // open: gt, lt
  or or_1 (ExtOp[0], comparator_1_eq, comparator_2_eq, comparator_3_eq);
  or or_2 (ExtOp[1], comparator_3_eq, comparator_4_eq);
  or or_3 (ALUASrc, comparator_6_eq, comparator_7_eq, comparator_8_eq);
  or or_4 (ALUBSrc[1], comparator_9_eq, comparator_10_eq, comparator_11_eq, comparator_12_eq, comparator_13_eq);
  or or_5 (ALUBSrc[0], comparator_14_eq, comparator_15_eq);
  or or_6 (RegWr, comparator_18_eq, comparator_19_eq, comparator_20_eq, comparator_21_eq, comparator_22_eq, comparator_23_eq, comparator_24_eq);
  Comparator #(.width(7)) comparator_25 (
    .a(opcode), .b(7'b0000011), .eq(comparator_25_eq), .lt(comparator_25_lt));  // open: gt
  Multiplexer #(.select(3), .width(3)) multiplexer_1 (
    .in0(3'b101), .in1(3'b110), .in2(3'b000), .in4(3'b001), .in5(3'b010), .out(MemOp), .sel(funct3),
    .en(comparator_25_eq));  // open: in3, in6, in7
  Comparator #(.width(7)) comparator_26 (.a(opcode), .b(7'b0100011), .eq(comparator_26_eq));  // open: gt, lt
  Multiplexer #(.select(3), .width(3)) multiplexer_2 (
    .in0(3'b101), .in1(3'b110), .in2(3'b000), .out(MemOp), .sel(funct3), .en(comparator_26_eq));  // open: in3, in4, in5, in6, in7
  Comparator #(.width(7)) comparator_27 (.a(opcode), .b(7'b1101111), .eq(comparator_27_eq));  // open: gt, lt
  Comparator #(.width(7)) comparator_28 (.a(opcode), .b(7'b1100111), .eq(comparator_28_eq));  // open: gt, lt
  Comparator #(.width(7)) comparator_29 (.a(opcode), .b(7'b1100011), .eq(comparator_29_eq));  // open: gt, lt
  Multiplexer #(.select(3), .width(3)) multiplexer_3 (
    .in0(3'b100), .in1(3'b101), .in4(3'b110), .in5(3'b111), .in6(3'b110), .in7(3'b111), .out(BandJ),
    .sel(funct3), .en(comparator_29_eq));  // open: in2, in3
  or or_7 (or_7_out, comparator_25_eq, comparator_26_eq);
  assign BandJ = comparator_27_eq ? 3'b001 : 3'bz;  // Controlled_Buffer controlled_buffer_1
  assign BandJ = comparator_28_eq ? 3'b010 : 3'bz;  // Controlled_Buffer controlled_buffer_2
  or or_8 (or_8_out, comparator_29_eq, comparator_28_eq, comparator_27_eq);
  not not_1 (not_1_out, or_8_out);
  assign BandJ = not_1_out ? 3'b000 : 3'bz;  // Controlled_Buffer controlled_buffer_3
  assign MemOp = not_2_out ? 3'b000 : 3'bz;  // Controlled_Buffer controlled_buffer_4
  not not_2 (not_2_out, or_7_out);
  Comparator #(.width(7)) comparator_30 (.a(opcode), .b(7'b0110111), .eq(comparator_30_eq));  // open: gt, lt
  Comparator #(.width(7)) comparator_31 (.a(opcode), .b(7'b0010011), .eq(comparator_31_eq));  // open: gt, lt
  Comparator #(.width(7)) comparator_32 (.a(opcode), .b(7'b0110011), .eq(comparator_32_eq));  // open: gt, lt
  Comparator #(.width(7)) comparator_33 (.a(opcode), .b(7'b1100011), .eq(comparator_33_eq));  // open: gt, lt
  and and_1 (and_1_out, comparator_31_eq, funct3[2], ~funct3[1], funct3[0], funct7[5]);  // AND_Gate
  and and_2 (and_2_out, comparator_32_eq, funct7[5]);
  and and_3 (and_3_out, comparator_31_eq, funct3[2]);
  and and_4 (and_4_out, comparator_32_eq, funct3[2]);
  and and_5 (and_5_out, comparator_31_eq, funct3[1]);
  and and_6 (and_6_out, comparator_32_eq, funct3[1]);
  and and_7 (and_7_out, comparator_31_eq, funct3[0]);
  and and_8 (and_8_out, comparator_32_eq, funct3[0]);
  and and_9 (and_9_out, comparator_33_eq, funct3[1]);
  or or_9 (ALUctr[3], comparator_30_eq, and_1_out, and_2_out);
  or or_10 (ALUctr[2], comparator_30_eq, and_3_out, and_4_out);
  or or_11 (ALUctr[1], comparator_30_eq, and_5_out, and_6_out, comparator_33_eq);
  or or_12 (ALUctr[0], comparator_30_eq, and_7_out, and_8_out, and_9_out);

  // Notes on the sheet:
  //   输入引脚
  //   请勿修改引脚名称、电路名称及电路封装外观
  //   提示：根据指令种类，把7位指令code用一位指令类型标志位来表示，再通过功能码来区分具体指令，生成控制信号。
  //   输出引脚
endmodule
