// Logisim project lab6.3.circ as structural Verilog: 17 circuits, main circuit main
module main (
  input  ReSet,
  input  [31:0] Init_Addr,
  input  clk,
  output [31:0] PC,
  output [31:0] IR,
  output [31:0] BusW,
  output [31:0] Din,
  output [15:0] Cycles,
  output Halt
);

  wire alu_1_zero, bandj_1_npcasrc, bandj_1_npcbsrc, clk_out, clk_t, not_2_out, \控制器_1_aluasrc ,
       \控制器_1_memtoreg , \控制器_1_memwr , \控制器_1_regwr ;
  wire [1:0] \控制器_1_alubsrc ;
  wire [2:0] idu_1_funct3, \控制器_1_bandj , \控制器_1_extop , \控制器_1_memop ;
  wire [3:0] \控制器_1_aluctr ;
  wire [6:0] idu_1_funct7, idu_1_opcode;
  wire [31:0] alu_1_s, dataram_1_dataout, idu_1_busa, idu_1_dataa, idu_1_datab, idu_1_imm;

  IFU ifu_1 (
    .CLK(clk_t), .Reset(ReSet), .NPCASrc(bandj_1_npcasrc), .NPCBSrc(bandj_1_npcbsrc),
    .Initial_Address(Init_Addr), .Imm(idu_1_imm), .BusA(idu_1_busa), .PC(PC), .halt(Halt));
  not not_1 (clk_t, clk_out);
  Clock u_clk (.out(clk_out));
  ROM #(.addrWidth(16), .dataWidth(32), .Select("high")) rom_1 (.addr(PC[17:2]), .data(IR), .sel(1'b1));
  \控制器  \u_控制器_1  (
    .opcode(idu_1_opcode), .ExtOp(\控制器_1_extop ), .RegWr(\控制器_1_regwr ), .BandJ(\控制器_1_bandj ),
    .funct3(idu_1_funct3), .ALUASrc(\控制器_1_aluasrc ), .ALUBSrc(\控制器_1_alubsrc ), .ALUctr(\控制器_1_aluctr ),
    .funct7(idu_1_funct7), .MemtoReg(\控制器_1_memtoreg ), .MemOp(\控制器_1_memop ), .MemWr(\控制器_1_memwr ),
    .Halt(Halt));
  BandJ bandj_1 (
    .BandJ(\控制器_1_bandj ), .NPCASrc(bandj_1_npcasrc), .Zero(alu_1_zero), .NPCBSrc(bandj_1_npcbsrc),
    .Result0(alu_1_s[0]));
  IDU idu_1 (
    .OpCode(idu_1_opcode), .ExtOp(\控制器_1_extop ), .RegWr(\控制器_1_regwr ), .Imm(idu_1_imm),
    .Funct3(idu_1_funct3), .ALUASrc(\控制器_1_aluasrc ), .ALUBSrc(\控制器_1_alubsrc ), .Funct7(idu_1_funct7),
    .CLK(clk_t), .IR(IR), .BusW(BusW), .PC(PC), .DataA(idu_1_dataa), .DataB(idu_1_datab), .BusA(idu_1_busa),
    .BusB(Din));
  ALU alu_1 (.A(idu_1_dataa), .B(idu_1_datab), .ALUctr(\控制器_1_aluctr ), .S(alu_1_s), .Zero(alu_1_zero));
  DataRAM dataram_1 (
    .Addr(alu_1_s[17:0]), .Din(Din), .CLK(clk_t), .CLR(1'b0), .WE(\控制器_1_memwr ), .MemOp(\控制器_1_memop ),
    .DataOut(dataram_1_dataout));  // open: AlignErr
  Multiplexer #(.width(32), .enable("false")) multiplexer_1 (
    .in0(alu_1_s), .in1(dataram_1_dataout), .out(BusW), .sel(\控制器_1_memtoreg ));
  // Probe on Cycles
  Counter #(.width(16), .max('hffff), .behavior("old")) \u_计数器  (
    .count(not_2_out), .Q(Cycles), .clk(clk_t), .clr(ReSet));  // open: load, D, carry, preset
  not not_2 (not_2_out, Halt);

  // Notes on the sheet:
  //   输入引脚
  //   contents of rom_1 (hex, n*v repeats v):
  //   4583 2058663 106613 d6c6b3 c686b3 b60663 160613 ff5ff06f d02223 c10537 fee50513 73 deade537 ead50513
  //   73
  //   请勿修改引脚名称、电路名称及电路封装外观
  //   指令存储器和数据存储器数据位都是32位，指令存储器编址以字为单位，数据存储器编址以字节为单位。
  //   引用取指令部件、取操作数部件、ALU部件、数据存储器、分支控制器、指令存储器等部件，完成单周期CPU设计。
  //   输出引脚
  //   状态元件的触发条件都设置成上升沿触发，时钟输入信号通过反相器输入。
  //   程序执行周期数
endmodule

module BandJ (
  input  [2:0] BandJ,
  input  Zero,
  input  Result0,
  output NPCASrc,
  output NPCBSrc
);

  wire not_1_out, not_2_out, not_3_out, not_4_out, not_5_out, or_1_out;

  not not_1 (not_1_out, 1'b0);
  Multiplexer #(.select(3), .enable("false")) multiplexer_1 (
    .in0(1'b0), .in1(1'b0), .in2(not_1_out), .in4(1'b0), .in5(1'b0), .in6(1'b0), .in7(1'b0), .out(NPCASrc),
    .sel(BandJ));  // open: in3
  not not_2 (not_2_out, 1'b0);
  not not_3 (not_3_out, 1'b0);
  not not_4 (not_4_out, Zero);
  or or_1 (or_1_out, Zero, not_5_out);
  not not_5 (not_5_out, Result0);
  Multiplexer #(.select(3), .enable("false")) multiplexer_2 (
    .in0(1'b0), .in1(not_2_out), .in2(not_3_out), .in4(Zero), .in5(not_4_out), .in6(Result0), .in7(or_1_out),
    .out(NPCBSrc), .sel(BandJ));  // open: in3

  // Notes on the sheet:
  //   BandJ: pull=down
  //   Zero: pull=down
  //   输入信号
  //   请勿修改引脚名称、电路名称及电路封装外观
  //   不要修改控制信号的编码定义、引脚名称和在布局中的位置。
  //   输出信号
endmodule

module IFU (
  input  [31:0] Initial_Address,
  input  [31:0] Imm,
  input  [31:0] BusA,
  input  CLK,
  input  Reset,
  input  halt,
  input  NPCASrc,
  input  NPCBSrc,
  output [31:0] PC
);

  wire and_1_out, not_1_out, or_1_out;
  wire [31:0] adder_1_out, multiplexer_1_out, multiplexer_2_out, multiplexer_3_out;

  Multiplexer #(.width(32), .enable("false")) multiplexer_1 (
    .in0(PC), .in1(BusA), .out(multiplexer_1_out), .sel(NPCASrc));
  Multiplexer #(.width(32), .enable("false")) multiplexer_2 (
    .in0(32'h4), .in1(Imm), .out(multiplexer_2_out), .sel(NPCBSrc));
  Adder #(.width(32)) adder_1 (.a(multiplexer_1_out), .b(multiplexer_2_out), .out(adder_1_out));  // open: cin, cout
  Register #(.width(32), .Select("low")) register_1 (.D(multiplexer_3_out), .Q(PC), .clk(and_1_out));  // open: en, clr
  Multiplexer #(.width(32), .enable("false")) multiplexer_3 (
    .in0(adder_1_out), .in1(Initial_Address), .out(multiplexer_3_out), .sel(Reset));
  and and_1 (and_1_out, CLK, or_1_out);
  or or_1 (or_1_out, not_1_out, Reset);
  not not_1 (not_1_out, halt);

  // Other names for the same wires on the sheet: Init_Addr[31:0] = Initial_Address

  // Notes on the sheet:
  //   Imm: pull=down
  //   BusA: pull=down
  //   NPCASrc: pull=down
  //   NPCBSrc: pull=down
  //   请勿修改引脚名称、电路名称及电路封装外观
  //   指令存储器256KB，数据位为32位，地址位为16位。PC寄存器数据宽度32位，片选信号高电平有效
  //   输入信号
  //   输出信号
endmodule

module \控制器  (
  input  [6:0] opcode,
  input  [2:0] funct3,
  input  [6:0] funct7,
  output [2:0] ExtOp,
  output RegWr,
  output [2:0] BandJ,
  output ALUASrc,
  output [1:0] ALUBSrc,
  output [3:0] ALUctr,
  output MemtoReg,
  output [2:0] MemOp,
  output MemWr,
  output Halt
);

  wire and_1_out, and_2_out, and_3_out, and_4_out, and_5_out, and_6_out, and_7_out, and_8_out, and_9_out,
       comparator_1_eq, comparator_2_eq, comparator_3_eq, comparator_4_eq, comparator_7_eq, comparator_8_eq,
       comparator_9_eq, comparator_10_eq, comparator_11_eq, comparator_12_eq, comparator_13_eq,
       comparator_14_eq, comparator_15_eq, comparator_16_eq, comparator_19_eq, comparator_20_eq,
       comparator_21_eq, comparator_22_eq, comparator_23_eq, comparator_24_eq, comparator_25_eq,
       comparator_26_eq, comparator_26_lt, comparator_27_eq, comparator_28_eq, comparator_29_eq,
       comparator_30_eq, comparator_31_eq, comparator_32_eq, comparator_33_eq, comparator_34_eq, not_1_out,
       not_2_out, or_7_out, or_8_out;

  Comparator #(.width(7)) comparator_1 (.a(opcode), .b(7'b0110111), .eq(comparator_1_eq));  // open: gt, lt
  Comparator #(.width(7)) comparator_2 (.a(opcode), .b(7'b0010111), .eq(comparator_2_eq));  // open: gt, lt
  Comparator #(.width(7)) comparator_3 (.a(opcode), .b(7'b1100011), .eq(comparator_3_eq));  // open: gt, lt
  Comparator #(.width(7)) comparator_4 (.a(opcode), .b(7'b0100011), .eq(comparator_4_eq));  // open: gt, lt
  Comparator #(.width(7)) comparator_5 (.a(opcode), .b(7'b1101111), .eq(ExtOp[2]));  // open: gt, lt
  Comparator #(.width(7)) comparator_6 (.a(opcode), .b(7'b1110011), .eq(Halt));  // open: gt, lt
  Comparator #(.width(7)) comparator_7 (.a(opcode), .b(7'b0010111), .eq(comparator_7_eq));  // open: gt, lt
  Comparator #(.width(7)) comparator_8 (.a(opcode), .b(7'b1101111), .eq(comparator_8_eq));  // open: gt, lt
  Comparator #(.width(7)) comparator_9 (.a(opcode), .b(7'b1100111), .eq(comparator_9_eq));  // open: gt, lt
  Comparator #(.width(7)) comparator_10 (.a(opcode), .b(7'b0110111), .eq(comparator_10_eq));  // open: gt, lt
  Comparator #(.width(7)) comparator_11 (.a(opcode), .b(7'b0010111), .eq(comparator_11_eq));  // open: gt, lt
  Comparator #(.width(7)) comparator_12 (.a(opcode), .b(7'b0010011), .eq(comparator_12_eq));  // open: gt, lt
  Comparator #(.width(7)) comparator_13 (.a(opcode), .b(7'b0000011), .eq(comparator_13_eq));  // open: gt, lt
  Comparator #(.width(7)) comparator_14 (.a(opcode), .b(7'b0100011), .eq(comparator_14_eq));  // open: gt, lt
  Comparator #(.width(7)) comparator_15 (.a(opcode), .b(7'b1101111), .eq(comparator_15_eq));  // open: gt, lt
  Comparator #(.width(7)) comparator_16 (.a(opcode), .b(7'b1100111), .eq(comparator_16_eq));  // open: gt, lt
  Comparator #(.width(7)) comparator_17 (.a(opcode), .b(7'b0000011), .eq(MemtoReg));  // open: gt, lt
  Comparator #(.width(7)) comparator_18 (.a(opcode), .b(7'b0100011), .eq(MemWr));  // open: gt, lt
  Comparator #(.width(7)) comparator_19 (.a(opcode), .b(7'b0000011), .eq(comparator_19_eq));  // open: gt, lt
  Comparator #(.width(7)) comparator_20 (.a(opcode), .b(7'b1100111), .eq(comparator_20_eq));  // open: gt, lt
  Comparator #(.width(7)) comparator_21 (.a(opcode), .b(7'b1101111), .eq(comparator_21_eq));  // open: gt, lt
  Comparator #(.width(7)) comparator_22 (.a(opcode), .b(7'b0110011), .eq(comparator_22_eq));  // open: gt, lt
  Comparator #(.width(7)) comparator_23 (.a(opcode), .b(7'b0010011), .eq(comparator_23_eq));  // open: gt, lt
  Comparator #(.width(7)) comparator_24 (.a(opcode), .b(7'b0010111), .eq(comparator_24_eq));  // open: gt, lt
  Comparator #(.width(7)) comparator_25 (.a(opcode), .b(7'b0110111), .eq(comparator_25_eq));  // open: gt, lt
  or or_1 (ExtOp[0], comparator_1_eq, comparator_2_eq, comparator_3_eq);
  or or_2 (ExtOp[1], comparator_3_eq, comparator_4_eq);
  or or_3 (ALUASrc, comparator_7_eq, comparator_8_eq, comparator_9_eq);
  or or_4 (ALUBSrc[1], comparator_10_eq, comparator_11_eq, comparator_12_eq, comparator_13_eq, comparator_14_eq);
  or or_5 (ALUBSrc[0], comparator_15_eq, comparator_16_eq);
  or or_6 (RegWr, comparator_19_eq, comparator_20_eq, comparator_21_eq, comparator_22_eq, comparator_23_eq, comparator_24_eq, comparator_25_eq);
  Comparator #(.width(7)) comparator_26 (
    .a(opcode), .b(7'b0000011), .eq(comparator_26_eq), .lt(comparator_26_lt));  // open: gt
  Multiplexer #(.select(3), .width(3)) multiplexer_1 (
    .in0(3'b101), .in1(3'b110), .in2(3'b000), .in4(3'b001), .in5(3'b010), .out(MemOp), .sel(funct3),
    .en(comparator_26_eq));  // open: in3, in6, in7
  Comparator #(.width(7)) comparator_27 (.a(opcode), .b(7'b0100011), .eq(comparator_27_eq));  // open: gt, lt
  Multiplexer #(.select(3), .width(3)) multiplexer_2 (
    .in0(3'b101), .in1(3'b110), .in2(3'b000), .out(MemOp), .sel(funct3), .en(comparator_27_eq));  // open: in3, in4, in5, in6, in7
  Comparator #(.width(7)) comparator_28 (.a(opcode), .b(7'b1101111), .eq(comparator_28_eq));  // open: gt, lt
  Comparator #(.width(7)) comparator_29 (.a(opcode), .b(7'b1100111), .eq(comparator_29_eq));  // open: gt, lt
  Comparator #(.width(7)) comparator_30 (.a(opcode), .b(7'b1100011), .eq(comparator_30_eq));  // open: gt, lt
  Multiplexer #(.select(3), .width(3)) multiplexer_3 (
    .in0(3'b100), .in1(3'b101), .in4(3'b110), .in5(3'b111), .in6(3'b110), .in7(3'b111), .out(BandJ),
    .sel(funct3), .en(comparator_30_eq));  // open: in2, in3
  or or_7 (or_7_out, comparator_26_eq, comparator_27_eq);
  assign BandJ = comparator_28_eq ? 3'b001 : 3'bz;  // Controlled_Buffer controlled_buffer_1
  assign BandJ = comparator_29_eq ? 3'b010 : 3'bz;  // Controlled_Buffer controlled_buffer_2
  or or_8 (or_8_out, comparator_30_eq, comparator_29_eq, comparator_28_eq);
  not not_1 (not_1_out, or_8_out);
  assign BandJ = not_1_out ? 3'b000 : 3'bz;  // Controlled_Buffer controlled_buffer_3
  assign MemOp = not_2_out ? 3'b000 : 3'bz;  // Controlled_Buffer controlled_buffer_4
  not not_2 (not_2_out, or_7_out);
  Comparator #(.width(7)) comparator_31 (.a(opcode), .b(7'b0110111), .eq(comparator_31_eq));  // open: gt, lt
  Comparator #(.width(7)) comparator_32 (.a(opcode), .b(7'b0010011), .eq(comparator_32_eq));  // open: gt, lt
  Comparator #(.width(7)) comparator_33 (.a(opcode), .b(7'b0110011), .eq(comparator_33_eq));  // open: gt, lt
  Comparator #(.width(7)) comparator_34 (.a(opcode), .b(7'b1100011), .eq(comparator_34_eq));  // open: gt, lt
  and and_1 (and_1_out, comparator_32_eq, funct3[2], ~funct3[1], funct3[0], funct7[5]);  // AND_Gate
  and and_2 (and_2_out, comparator_33_eq, funct7[5]);
  and and_3 (and_3_out, comparator_32_eq, funct3[2]);
  and and_4 (and_4_out, comparator_33_eq, funct3[2]);
  and and_5 (and_5_out, comparator_32_eq, funct3[1]);
  and and_6 (and_6_out, comparator_33_eq, funct3[1]);
  and and_7 (and_7_out, comparator_32_eq, funct3[0]);
  and and_8 (and_8_out, comparator_33_eq, funct3[0]);
  and and_9 (and_9_out, comparator_34_eq, funct3[1]);
  or or_9 (ALUctr[3], comparator_31_eq, and_1_out, and_2_out);
  or or_10 (ALUctr[2], comparator_31_eq, and_3_out, and_4_out);
  or or_11 (ALUctr[1], comparator_31_eq, and_5_out, and_6_out, comparator_34_eq);
  or or_12 (ALUctr[0], comparator_31_eq, and_7_out, and_8_out, and_9_out);

  // Notes on the sheet:
  //   输入引脚
  //   请勿修改引脚名称、电路名称及电路封装外观
  //   提示：根据指令种类，把7位指令code用一位指令类型标志位来表示，再通过功能码来区分具体指令，生成控制信号。
  //   输出引脚
endmodule

module IDU (
  input  [31:0] IR,
  input  [31:0] BusW,
  input  [31:0] PC,
  input  [2:0] ExtOp,
  input  RegWr,
  input  ALUASrc,
  input  [1:0] ALUBSrc,
  input  CLK,
  output [31:0] DataA,
  output [31:0] DataB,
  output [31:0] BusA,
  output [31:0] BusB,
  output [6:0] OpCode,
  output [31:0] Imm,
  output [2:0] Funct3,
  output [6:0] Funct7
);

  \立即数扩展器  \u_立即数扩展器_1  (.Instr(IR), .Extop(ExtOp), .imm(Imm));
  RegFile regfile_1 (
    .R1_num(IR[19:15]), .R2_num(IR[24:20]), .Write_Reg_num(IR[11:7]), .Write_Enable(RegWr), .Clock(CLK),
    .Din(BusW), .Reg1Out(BusA), .Reg2Out(BusB));
  Multiplexer #(.width(32), .enable("false")) multiplexer_1 (.in0(BusA), .in1(PC), .out(DataA), .sel(ALUASrc));
  Multiplexer #(.select(2), .width(32), .enable("false")) multiplexer_2 (
    .in0(BusB), .in1(32'h4), .in2(Imm), .out(DataB), .sel(ALUBSrc));  // open: in3

  assign Funct3 = IR[14:12];
  assign Funct7 = IR[31:25];
  assign OpCode = IR[6:0];

  // Other names for the same wires on the sheet: op[6:0] = IR[6:0]

  // Notes on the sheet:
  //   ALUASrc: pull=down
  //   ALUBSrc: pull=down
  //   PC: pull=down
  //   BusW: pull=down
  //   ExtOp: pull=down
  //   RegWr: pull=down
  //   输入信号
  //   为了后续实验中的引用，不要修改ALUASrc、ALUBSrc和EXtOP编码定义。
  //   请勿修改引脚名称、电路名称及电路封装外观
  //   输出信号
  //   修改寄存器堆电路设计，0号寄存器始终为0。
endmodule

module RegFile (
  input  [4:0] R1_num,
  input  [4:0] R2_num,
  input  [4:0] Write_Reg_num,
  input  [31:0] Din,
  input  Write_Enable,
  input  Clock,
  output [31:0] Reg1Out,
  output [31:0] Reg2Out
);

  wire and_1_out, and_2_out, and_3_out, and_4_out, and_5_out, and_6_out, and_7_out, and_8_out, and_9_out,
       and_10_out, and_11_out, and_12_out, and_13_out, and_14_out, and_15_out, and_16_out, and_17_out,
       and_18_out, and_19_out, and_20_out, and_21_out, and_22_out, and_23_out, and_24_out, and_25_out,
       and_26_out, and_27_out, and_28_out, and_29_out, and_30_out, and_31_out, and_32_out, decoder_1_out0,
       decoder_1_out1, decoder_1_out2, decoder_1_out3, decoder_1_out4, decoder_1_out5, decoder_1_out6,
       decoder_1_out7, decoder_1_out8, decoder_1_out9, decoder_1_out10, decoder_1_out11, decoder_1_out12,
       decoder_1_out13, decoder_1_out14, decoder_1_out15, decoder_1_out16, decoder_1_out17, decoder_1_out18,
       decoder_1_out19, decoder_1_out20, decoder_1_out21, decoder_1_out22, decoder_1_out23, decoder_1_out24,
       decoder_1_out25, decoder_1_out26, decoder_1_out27, decoder_1_out28, decoder_1_out29, decoder_1_out30,
       decoder_1_out31;
  wire [31:0] _1_q, _2_q, _3_q, _4_q, _5_q, _6_q, _7_q, _8_q, _9_q, register_1_q, register_2_q, register_3_q,
       register_4_q, register_5_q, register_6_q, register_7_q, register_8_q, register_9_q, register_10_q,
       register_11_q, register_12_q, register_13_q, register_14_q, register_15_q, register_16_q,
       register_17_q, register_18_q, register_19_q, register_20_q, register_21_q, register_22_q;

  Decoder #(.select(5), .enable("false")) decoder_1 (
    .out0(decoder_1_out0), .out1(decoder_1_out1), .out2(decoder_1_out2), .out3(decoder_1_out3),
    .out4(decoder_1_out4), .out5(decoder_1_out5), .out6(decoder_1_out6), .out7(decoder_1_out7),
    .out8(decoder_1_out8), .out9(decoder_1_out9), .out10(decoder_1_out10), .out11(decoder_1_out11),
    .out12(decoder_1_out12), .out13(decoder_1_out13), .out14(decoder_1_out14), .out15(decoder_1_out15),
    .out16(decoder_1_out16), .out17(decoder_1_out17), .out18(decoder_1_out18), .out19(decoder_1_out19),
    .out20(decoder_1_out20), .out21(decoder_1_out21), .out22(decoder_1_out22), .out23(decoder_1_out23),
    .out24(decoder_1_out24), .out25(decoder_1_out25), .out26(decoder_1_out26), .out27(decoder_1_out27),
    .out28(decoder_1_out28), .out29(decoder_1_out29), .out30(decoder_1_out30), .out31(decoder_1_out31),
    .sel(Write_Reg_num));
  and and_1 (and_1_out, decoder_1_out0, Write_Enable);
  and and_2 (and_2_out, decoder_1_out1, Write_Enable);
  and and_3 (and_3_out, decoder_1_out2, Write_Enable);
  and and_4 (and_4_out, decoder_1_out3, Write_Enable);
  and and_5 (and_5_out, decoder_1_out4, Write_Enable);
  and and_6 (and_6_out, decoder_1_out5, Write_Enable);
  and and_7 (and_7_out, decoder_1_out6, Write_Enable);
  and and_8 (and_8_out, decoder_1_out7, Write_Enable);
  and and_9 (and_9_out, decoder_1_out8, Write_Enable);
  and and_10 (and_10_out, decoder_1_out9, Write_Enable);
  and and_11 (and_11_out, decoder_1_out10, Write_Enable);
  and and_12 (and_12_out, decoder_1_out11, Write_Enable);
  and and_13 (and_13_out, decoder_1_out12, Write_Enable);
  and and_14 (and_14_out, decoder_1_out13, Write_Enable);
  and and_15 (and_15_out, decoder_1_out14, Write_Enable);
  and and_16 (and_16_out, decoder_1_out15, Write_Enable);
  and and_17 (and_17_out, decoder_1_out16, Write_Enable);
  and and_18 (and_18_out, decoder_1_out17, Write_Enable);
  and and_19 (and_19_out, decoder_1_out18, Write_Enable);
  and and_20 (and_20_out, decoder_1_out19, Write_Enable);
  and and_21 (and_21_out, decoder_1_out20, Write_Enable);
  and and_22 (and_22_out, decoder_1_out21, Write_Enable);
  and and_23 (and_23_out, decoder_1_out22, Write_Enable);
  and and_24 (and_24_out, decoder_1_out23, Write_Enable);
  and and_25 (and_25_out, decoder_1_out24, Write_Enable);
  and and_26 (and_26_out, decoder_1_out25, Write_Enable);
  and and_27 (and_27_out, decoder_1_out26, Write_Enable);
  and and_28 (and_28_out, decoder_1_out27, Write_Enable);
  and and_29 (and_29_out, decoder_1_out28, Write_Enable);
  and and_30 (and_30_out, decoder_1_out29, Write_Enable);
  and and_31 (and_31_out, decoder_1_out30, Write_Enable);
  and and_32 (and_32_out, decoder_1_out31, Write_Enable);
  Register #(.width(32), .Select("low")) _0 (.D(Din), .en(and_1_out), .clk(Clock));  // open: Q, clr
  Register #(.width(32), .Select("low")) _1 (.D(Din), .en(and_2_out), .Q(_1_q), .clk(Clock));  // open: clr
  Register #(.width(32), .Select("low")) _2 (.D(Din), .en(and_3_out), .Q(_2_q), .clk(Clock));  // open: clr
  Register #(.width(32), .Select("low")) _3 (.D(Din), .en(and_4_out), .Q(_3_q), .clk(Clock));  // open: clr
  Register #(.width(32), .Select("low")) _4 (.D(Din), .en(and_5_out), .Q(_4_q), .clk(Clock));  // open: clr
  Register #(.width(32), .Select("low")) _5 (.D(Din), .en(and_6_out), .Q(_5_q), .clk(Clock));  // open: clr
  Register #(.width(32), .Select("low")) _6 (.D(Din), .en(and_7_out), .Q(_6_q), .clk(Clock));  // open: clr
  Register #(.width(32), .Select("low")) _7 (.D(Din), .en(and_8_out), .Q(_7_q), .clk(Clock));  // open: clr
  Register #(.width(32), .Select("low")) _8 (.D(Din), .en(and_9_out), .Q(_8_q), .clk(Clock));  // open: clr
  Register #(.width(32), .Select("low")) _9 (.D(Din), .en(and_10_out), .Q(_9_q), .clk(Clock));  // open: clr
  Register #(.width(32), .Select("low")) register_1 (
    .D(Din), .en(and_11_out), .Q(register_1_q), .clk(Clock));  // open: clr
  Register #(.width(32), .Select("low")) register_2 (
    .D(Din), .en(and_12_out), .Q(register_2_q), .clk(Clock));  // open: clr
  Register #(.width(32), .Select("low")) register_3 (
    .D(Din), .en(and_13_out), .Q(register_3_q), .clk(Clock));  // open: clr
  Register #(.width(32), .Select("low")) register_4 (
    .D(Din), .en(and_14_out), .Q(register_4_q), .clk(Clock));  // open: clr
  Register #(.width(32), .Select("low")) register_5 (
    .D(Din), .en(and_15_out), .Q(register_5_q), .clk(Clock));  // open: clr
  Register #(.width(32), .Select("low")) register_6 (
    .D(Din), .en(and_16_out), .Q(register_6_q), .clk(Clock));  // open: clr
  Register #(.width(32), .Select("low")) register_7 (
    .D(Din), .en(and_17_out), .Q(register_7_q), .clk(Clock));  // open: clr
  Register #(.width(32), .Select("low")) register_8 (
    .D(Din), .en(and_18_out), .Q(register_8_q), .clk(Clock));  // open: clr
  Register #(.width(32), .Select("low")) register_9 (
    .D(Din), .en(and_19_out), .Q(register_9_q), .clk(Clock));  // open: clr
  Register #(.width(32), .Select("low")) register_10 (
    .D(Din), .en(and_20_out), .Q(register_10_q), .clk(Clock));  // open: clr
  Register #(.width(32), .Select("low")) register_11 (
    .D(Din), .en(and_21_out), .Q(register_11_q), .clk(Clock));  // open: clr
  Register #(.width(32), .Select("low")) register_12 (
    .D(Din), .en(and_22_out), .Q(register_12_q), .clk(Clock));  // open: clr
  Register #(.width(32), .Select("low")) register_13 (
    .D(Din), .en(and_23_out), .Q(register_13_q), .clk(Clock));  // open: clr
  Register #(.width(32), .Select("low")) register_14 (
    .D(Din), .en(and_24_out), .Q(register_14_q), .clk(Clock));  // open: clr
  Register #(.width(32), .Select("low")) register_15 (
    .D(Din), .en(and_25_out), .Q(register_15_q), .clk(Clock));  // open: clr
  Register #(.width(32), .Select("low")) register_16 (
    .D(Din), .en(and_26_out), .Q(register_16_q), .clk(Clock));  // open: clr
  Register #(.width(32), .Select("low")) register_17 (
    .D(Din), .en(and_27_out), .Q(register_17_q), .clk(Clock));  // open: clr
  Register #(.width(32), .Select("low")) register_18 (
    .D(Din), .en(and_28_out), .Q(register_18_q), .clk(Clock));  // open: clr
  Register #(.width(32), .Select("low")) register_19 (
    .D(Din), .en(and_29_out), .Q(register_19_q), .clk(Clock));  // open: clr
  Register #(.width(32), .Select("low")) register_20 (
    .D(Din), .en(and_30_out), .Q(register_20_q), .clk(Clock));  // open: clr
  Register #(.width(32), .Select("low")) register_21 (
    .D(Din), .en(and_31_out), .Q(register_21_q), .clk(Clock));  // open: clr
  Register #(.width(32), .Select("low")) register_22 (
    .D(Din), .en(and_32_out), .Q(register_22_q), .clk(Clock));  // open: clr
  Multiplexer #(.select(5), .width(32), .enable("false")) multiplexer_1 (
    .in0({32{1'b0}}), .in1(_1_q), .in2(_2_q), .in3(_3_q), .in4(_4_q), .in5(_5_q), .in6(_6_q), .in7(_7_q),
    .in8(_8_q), .in9(_9_q), .in10(register_1_q), .in11(register_2_q), .in12(register_3_q),
    .in13(register_4_q), .in14(register_5_q), .in15(register_6_q), .in16(register_7_q), .in17(register_8_q),
    .in18(register_9_q), .in19(register_10_q), .in20(register_11_q), .in21(register_12_q),
    .in22(register_13_q), .in23(register_14_q), .in24(register_15_q), .in25(register_16_q),
    .in26(register_17_q), .in27(register_18_q), .in28(register_19_q), .in29(register_20_q),
    .in30(register_21_q), .in31(register_22_q), .out(Reg1Out), .sel(R1_num));
  Multiplexer #(.select(5), .width(32), .enable("false")) multiplexer_2 (
    .in0({32{1'b0}}), .in1(_1_q), .in2(_2_q), .in3(_3_q), .in4(_4_q), .in5(_5_q), .in6(_6_q), .in7(_7_q),
    .in8(_8_q), .in9(_9_q), .in10(register_1_q), .in11(register_2_q), .in12(register_3_q),
    .in13(register_4_q), .in14(register_5_q), .in15(register_6_q), .in16(register_7_q), .in17(register_8_q),
    .in18(register_9_q), .in19(register_10_q), .in20(register_11_q), .in21(register_12_q),
    .in22(register_13_q), .in23(register_14_q), .in24(register_15_q), .in25(register_16_q),
    .in26(register_17_q), .in27(register_18_q), .in28(register_19_q), .in29(register_20_q),
    .in30(register_21_q), .in31(register_22_q), .out(Reg2Out), .sel(R2_num));

  // Other names for the same wires on the sheet: CLK = Clock; RA[4:0] = R1_num; RB[4:0] = R2_num; RDA[31:0] = Reg1Out;
  //   RDB[31:0] = Reg2Out; RW[4:0] = Write_Reg_num; WE = Write_Enable

  // Notes on the sheet:
  //   输入引脚
  //   请勿修改引脚名称、电路名称及电路封装外观
  //   提示：使用译码器、多路选择器和32位寄存器及逻辑门实现寄存器堆，禁止直接使用存储器组件。
  //   输出引脚
endmodule

module \立即数扩展器  (
  input  [31:0] Instr,
  input  [2:0] Extop,
  output [31:0] imm
);

  wire [11:0] bit_extender_4_out;
  wire [19:0] bit_extender_1_out, bit_extender_2_out, bit_extender_3_out;

  assign bit_extender_1_out = {{19{Instr[31]}}, Instr[31]};  // Bit_Extender bit_extender_1
  assign bit_extender_2_out = {{19{Instr[31]}}, Instr[31]};  // Bit_Extender bit_extender_2
  assign bit_extender_3_out = {{19{Instr[31]}}, Instr[31]};  // Bit_Extender bit_extender_3
  assign bit_extender_4_out = {{11{Instr[31]}}, Instr[31]};  // Bit_Extender bit_extender_4
  Multiplexer #(.select(3), .width(32), .enable("false")) multiplexer_1 (
    .in0({bit_extender_1_out, Instr[31:20]}), .in1({Instr[31:12], {12{1'b0}}}),
    .in2({bit_extender_2_out, Instr[31:25], Instr[11:7]}),
    .in3({bit_extender_3_out, Instr[7], Instr[30:25], Instr[11:8], 1'b0}),
    .in4({bit_extender_4_out, Instr[19:12], Instr[20], Instr[30:21], 1'b0}), .out(imm), .sel(Extop));  // open: in5, in6, in7

  // Notes on the sheet:
  //   Instr: pull=down
  //   Extop: pull=down
  //   输入引脚
  //   输出引脚
endmodule

module DataRAM (
  input  CLK,
  input  CLR,
  input  WE,
  input  [2:0] MemOp,
  input  [17:0] Addr,
  input  [31:0] Din,
  output AlignErr,
  output [31:0] DataOut
);

  wire and_1_out, and_2_out, and_3_out, and_4_out, or_1_out, or_2_out, or_3_out, or_4_out;
  wire [3:0] SEL;
  wire [7:0] multiplexer_1_out, multiplexer_2_out, multiplexer_3_out, multiplexer_5_out, multiplexer_6_out,
       multiplexer_9_out, multiplexer_11_out;
  wire [17:0] adder_1_out, adder_2_out, adder_3_out, adder_4_out, multiplexer_4_out, multiplexer_8_out,
       multiplexer_10_out, multiplexer_12_out;
  wire [31:0] bit_extender_1_out, bit_extender_2_out, bit_extender_3_out, bit_extender_4_out, Result;

  SEL sel_1 (
    .Mem2(MemOp[2]), .Mem1(MemOp[1]), .Mem0(MemOp[0]), .Addr1(Addr[1]), .Addr0(Addr[0]), .Sel3(SEL[3]),
    .Sel2(SEL[2]), .Sel1(SEL[1]), .Sel0(SEL[0]));
  Multiplexer #(.select(4), .width(8), .enable("false")) multiplexer_1 (
    .in8(Din[7:0]), .in12(Din[15:8]), .in15(Din[31:24]), .out(multiplexer_1_out), .sel(SEL));  // open: in0, in1, in2, in3, in4, in5, in6, in7, in9, in10, in11, in13, in14
  and and_1 (and_1_out, SEL[3], WE);
  Multiplexer #(.select(4), .width(8), .enable("false")) multiplexer_2 (
    .in1(Result[7:0]), .in2(Result[15:8]), .in4(Result[23:16]), .in8(Result[31:24]), .out(multiplexer_2_out),
    .sel(SEL));  // open: in0, in3, in5, in6, in7, in9, in10, in11, in12, in13, in14, in15
  nor nor_1 (AlignErr, SEL[3], SEL[2], SEL[1], SEL[0]);
  Adder #(.width(18)) adder_1 (.a(Addr), .b(18'h3), .out(adder_1_out));  // open: cin, cout
  Adder #(.width(18)) adder_2 (.a(Addr), .b(18'h1), .out(adder_2_out));  // open: cin, cout
  or or_1 (or_1_out, SEL[3], WE);
  Multiplexer #(.select(4), .width(8), .enable("false")) multiplexer_3 (
    .in3(Result[7:0]), .in12(Result[23:16]), .out(multiplexer_3_out), .sel(SEL));  // open: in0, in1, in2, in4, in5, in6, in7, in8, in9, in10, in11, in13, in14, in15
  Multiplexer #(.select(4), .width(18), .enable("false")) multiplexer_4 (
    .in8(Addr), .in12(adder_2_out), .in15(adder_1_out), .out(multiplexer_4_out), .sel(SEL));  // open: in0, in1, in2, in3, in4, in5, in6, in7, in9, in10, in11, in13, in14
  RAM #(.addrWidth(18), .bus("separate"), .Select("high"), .simpleMode("false")) ram_1 (
    .addr(multiplexer_4_out), .din(multiplexer_1_out), .data(Result[31:24]), .str(and_1_out), .sel(or_1_out),
    .clk(CLK), .clr(CLR));  // open: ld
  Multiplexer #(.select(4), .width(8), .enable("false")) multiplexer_5 (
    .in3(Result[15:8]), .in12(Result[31:24]), .out(multiplexer_5_out), .sel(SEL));  // open: in0, in1, in2, in4, in5, in6, in7, in8, in9, in10, in11, in13, in14, in15
  Multiplexer #(.select(4), .width(8), .enable("false")) multiplexer_6 (
    .in4(Din[7:0]), .in12(Din[7:0]), .in15(Din[23:16]), .out(multiplexer_6_out), .sel(SEL));  // open: in0, in1, in2, in3, in5, in6, in7, in8, in9, in10, in11, in13, in14
  and and_2 (and_2_out, SEL[2], WE);
  Adder #(.width(18)) adder_3 (.a(Addr), .b(18'h2), .out(adder_3_out));  // open: cin, cout
  or or_2 (or_2_out, SEL[2], WE);
  assign bit_extender_1_out = {{16{1'b0}}, {multiplexer_5_out, multiplexer_3_out}};  // Bit_Extender bit_extender_1
  assign bit_extender_2_out = {{16{multiplexer_5_out[7]}}, {multiplexer_5_out, multiplexer_3_out}};  // Bit_Extender bit_extender_2
  assign bit_extender_3_out = {{24{1'b0}}, multiplexer_2_out};  // Bit_Extender bit_extender_3
  assign bit_extender_4_out = {{24{multiplexer_2_out[7]}}, multiplexer_2_out};  // Bit_Extender bit_extender_4
  RAM #(.addrWidth(18), .bus("separate"), .Select("high"), .simpleMode("false")) ram_2 (
    .addr(multiplexer_8_out), .din(multiplexer_6_out), .data(Result[23:16]), .str(and_2_out), .sel(or_2_out),
    .clk(CLK), .clr(CLR));  // open: ld
  Multiplexer #(.select(3), .width(32), .enable("false")) multiplexer_7 (
    .in0(Result), .in1(bit_extender_3_out), .in2(bit_extender_1_out), .in5(bit_extender_4_out),
    .in6(bit_extender_2_out), .out(DataOut), .sel(MemOp));  // open: in3, in4, in7
  Multiplexer #(.select(4), .width(18), .enable("false")) multiplexer_8 (
    .in4(Addr), .in12(Addr), .in15(adder_3_out), .out(multiplexer_8_out), .sel(SEL));  // open: in0, in1, in2, in3, in5, in6, in7, in8, in9, in10, in11, in13, in14
  Multiplexer #(.select(4), .width(8), .enable("false")) multiplexer_9 (
    .in2(Din[7:0]), .in3(Din[15:8]), .in15(Din[15:8]), .out(multiplexer_9_out), .sel(SEL));  // open: in0, in1, in4, in5, in6, in7, in8, in9, in10, in11, in12, in13, in14
  or or_3 (or_3_out, SEL[1], WE);
  and and_3 (and_3_out, SEL[1], WE);
  Adder #(.width(18)) adder_4 (.a(Addr), .b(18'h1), .out(adder_4_out));  // open: cin, cout
  RAM #(.addrWidth(18), .bus("separate"), .Select("high"), .simpleMode("false")) ram_3 (
    .addr(multiplexer_10_out), .din(multiplexer_9_out), .data(Result[15:8]), .str(and_3_out), .sel(or_3_out),
    .clk(CLK), .clr(CLR));  // open: ld
  Multiplexer #(.select(4), .width(18), .enable("false")) multiplexer_10 (
    .in2(Addr), .in3(adder_4_out), .in15(adder_4_out), .out(multiplexer_10_out), .sel(SEL));  // open: in0, in1, in4, in5, in6, in7, in8, in9, in10, in11, in12, in13, in14
  Multiplexer #(.select(4), .width(8), .enable("false")) multiplexer_11 (
    .in1(Din[7:0]), .in3(Din[7:0]), .in15(Din[7:0]), .out(multiplexer_11_out), .sel(SEL));  // open: in0, in2, in4, in5, in6, in7, in8, in9, in10, in11, in12, in13, in14
  and and_4 (and_4_out, SEL[0], WE);
  or or_4 (or_4_out, SEL[0], WE);
  RAM #(.addrWidth(18), .bus("separate"), .Select("high"), .simpleMode("false")) ram_4 (
    .addr(multiplexer_12_out), .din(multiplexer_11_out), .data(Result[7:0]), .str(and_4_out), .sel(or_4_out),
    .clk(CLK), .clr(CLR));  // open: ld
  Multiplexer #(.select(4), .width(18), .enable("false")) multiplexer_12 (
    .in1(Addr), .in3(Addr), .in15(Addr), .out(multiplexer_12_out), .sel(SEL));  // open: in0, in2, in4, in5, in6, in7, in8, in9, in10, in11, in12, in13, in14

  // Other names for the same wires on the sheet: Dout[31:0] = DataOut

  // Notes on the sheet:
  //   输入引脚
  //   请勿修改引脚名称、电路名称及电路封装外观
  //   为了后续实验中的引用，不要修改MemOp的编码定义、引脚名称和在布局中的位置。
  //   32位数据存储器，按字节分4片存储，可按照字节、半字和字进行存储；读取字节或半字时，支持0扩展和符号位扩展。
  //   输出引脚
endmodule

module ALU (
  input  [3:0] ALUctr,
  input  [31:0] A,
  input  [31:0] B,
  output Zero,
  output [31:0] S
);

  wire adder32_1_cout, adder32_1_of, adder32_1_sf, aluctrl_1_alctr, aluctrl_1_sftctr, aluctrl_1_sigctr,
       aluctrl_1_subctr, multiplexer_1_out, xor_3_out, xor_4_out;
  wire [2:0] aluctrl_1_opctr;
  wire [31:0] adder32_1_s, and_1_out, bit_extender_1_out, bit_extender_2_out, or_1_out, shifter32_1_dataout,
       xor_1_out, xor_2_out;

  assign bit_extender_1_out = {{31{aluctrl_1_subctr}}, aluctrl_1_subctr};  // Bit_Extender bit_extender_1
  assign xor_1_out = B ^ bit_extender_1_out;  // XOR_Gate xor_1, 32 bits wide
  Adder32 adder32_1 (
    .OF(adder32_1_of), .SF(adder32_1_sf), .ZF(Zero), .X(A), .Y(xor_1_out), .Cin(aluctrl_1_subctr),
    .S(adder32_1_s), .Cout(adder32_1_cout));  // open: CF
  assign and_1_out = A & B;  // AND_Gate and_1, 32 bits wide
  assign or_1_out = A | B;  // OR_Gate or_1, 32 bits wide
  assign xor_2_out = A ^ B;  // XOR_Gate xor_2, 32 bits wide
  Shifter32 shifter32_1 (
    .DataIn(A), .shamt(B[4:0]), .L_R(aluctrl_1_sftctr), .A_L(aluctrl_1_alctr), .DataOut(shifter32_1_dataout));
  ALUctrl aluctrl_1 (
    .SUBctr(aluctrl_1_subctr), .SFTctr(aluctrl_1_sftctr), .SIGctr(aluctrl_1_sigctr), .ALctr(aluctrl_1_alctr),
    .OPctr(aluctrl_1_opctr), .ALUctr(ALUctr));
  xor xor_3 (xor_3_out, aluctrl_1_subctr, adder32_1_cout);
  Multiplexer #(.enable("false")) multiplexer_1 (
    .in0(xor_3_out), .in1(xor_4_out), .out(multiplexer_1_out), .sel(aluctrl_1_sigctr));
  xor xor_4 (xor_4_out, adder32_1_of, adder32_1_sf);
  Multiplexer #(.select(3), .width(32), .enable("false")) multiplexer_2 (
    .in0(adder32_1_s), .in1(and_1_out), .in2(or_1_out), .in3(xor_2_out), .in4(shifter32_1_dataout), .in5(B),
    .in6(bit_extender_2_out), .out(S), .sel(aluctrl_1_opctr));  // open: in7
  assign bit_extender_2_out = {{31{1'b0}}, multiplexer_1_out};  // Bit_Extender bit_extender_2
  // Probe on A
  // Probe on B
  // Probe on S

  // Other names for the same wires on the sheet: Result[31:0] = S

  // Notes on the sheet:
  //   ALUctr: pull=down
  //   A: pull=down
  //   B: pull=down
  //   输入引脚
  //   请勿修改引脚名称、电路名称及电路封装外观
  //   提示：使用32位并行加法器子电路、桶形移位器、ALU控制子电路实现32位ALU
  //   功能说明:32位ALU，输入32位操作数A、B，4位控制信号ALUctr，输出32位结果Reseult和1位Zero标志位
  //   输出引脚
  //   操作数和结果
endmodule

module ALUctrl (
  input  [3:0] ALUctr,
  output SUBctr,
  output SFTctr,
  output SIGctr,
  output ALctr,
  output [2:0] OPctr
);

  wire and_1_out, and_2_out, and_3_out, and_4_out, and_5_out, and_6_out, and_7_out, and_8_out, and_9_out,
       and_10_out, and_11_out, and_12_out, and_13_out, and_14_out, and_15_out, and_16_out, not_1_out,
       not_2_out, not_3_out, not_4_out;

  not not_1 (not_1_out, ALUctr[1]);
  not not_2 (not_2_out, ALUctr[3]);
  not not_3 (not_3_out, ALUctr[2]);
  not not_4 (not_4_out, ALUctr[0]);
  and and_1 (and_1_out, not_4_out, ALUctr[1], not_3_out, not_2_out);
  and and_2 (and_2_out, ALUctr[0], ALUctr[1], not_3_out, not_2_out);
  and and_3 (and_3_out, not_4_out, not_1_out, not_3_out, ALUctr[3]);
  and and_4 (and_4_out, ALUctr[0], not_1_out, not_3_out, not_2_out);
  and and_5 (and_5_out, not_4_out, ALUctr[1], not_3_out, not_2_out);
  and and_6 (and_6_out, ALUctr[0], ALUctr[1], not_3_out, not_2_out);
  and and_7 (and_7_out, ALUctr[0], not_1_out, ALUctr[2], not_2_out);
  and and_8 (and_8_out, ALUctr[0], not_1_out, ALUctr[2], ALUctr[3]);
  and and_9 (and_9_out, ALUctr[0], ALUctr[1], ALUctr[2], ALUctr[3]);
  and and_10 (and_10_out, not_4_out, ALUctr[1], not_3_out, not_2_out);
  and and_11 (and_11_out, ALUctr[0], ALUctr[1], not_3_out, not_2_out);
  and and_12 (and_12_out, not_4_out, not_1_out, ALUctr[2], not_2_out);
  and and_13 (and_13_out, not_4_out, ALUctr[1], ALUctr[2], not_2_out);
  and and_14 (and_14_out, not_4_out, not_1_out, ALUctr[2], not_2_out);
  and and_15 (and_15_out, ALUctr[0], ALUctr[1], ALUctr[2], not_2_out);
  and and_16 (and_16_out, ALUctr[0], ALUctr[1], ALUctr[2], ALUctr[3]);
  or or_1 (SUBctr, and_1_out, and_2_out, and_3_out);
  and and_17 (SIGctr, not_4_out, ALUctr[1], not_3_out, not_2_out);
  and and_18 (ALctr, ALUctr[0], not_1_out, ALUctr[2], ALUctr[3]);
  and and_19 (SFTctr, ALUctr[0], not_1_out, not_3_out, not_2_out);
  or or_2 (OPctr[2], and_4_out, and_5_out, and_6_out, and_7_out, and_8_out, and_9_out);
  or or_3 (OPctr[1], and_10_out, and_11_out, and_12_out, and_13_out);
  or or_4 (OPctr[0], and_14_out, and_15_out, and_16_out);

  // Other names for the same wires on the sheet: LRctr = SFTctr

  // Notes on the sheet:
  //   输入引脚
  //   ALU操作控制信号生成部件
  //   输出引脚
endmodule

module Adder32 (
  input  Cin,
  input  [31:0] X,
  input  [31:0] Y,
  output CF,
  output Cout,
  output OF,
  output SF,
  output [31:0] S,
  output ZF
);

  wire adder16_2_c16, and_1_out, and_2_out, and_3_out, not_1_out, not_2_out, or_2_out, or_3_out;

  or or_1 (OF, and_1_out, and_2_out);
  and and_1 (and_1_out, S[31], not_1_out);
  not not_1 (not_1_out, or_3_out);
  not not_2 (not_2_out, S[31]);
  and and_2 (and_2_out, not_2_out, and_3_out);
  or or_2 (or_2_out, S[0], S[1], S[2], S[3], S[4], S[5], S[6], S[7], S[8], S[9], S[10], S[11], S[12], S[13], S[14], S[15], S[16], S[17], S[18], S[19], S[20], S[21], S[22], S[23], S[24], S[25], S[26], S[27], S[28], S[29], S[30], S[31]);
  not not_3 (ZF, or_2_out);
  xor xor_1 (CF, Cout, Cin);
  or or_3 (or_3_out, Y[31], X[31]);
  and and_3 (and_3_out, Y[31], X[31]);
  // Probe on X
  // Probe on Y
  // Probe on S
  Adder16 adder16_1 (.X(X[31:16]), .Y(Y[31:16]), .C0(adder16_2_c16), .S(S[31:16]), .C16(Cout));  // open: Pg, Gg
  Adder16 adder16_2 (.X(X[15:0]), .Y(Y[15:0]), .C0(Cin), .S(S[15:0]), .C16(adder16_2_c16));  // open: Pg, Gg

  assign SF = S[31];

  // Notes on the sheet:
  //   X: pull=down
  //   Cin: pull=down
  //   Y: pull=down
  //   输入引脚区
  //   输出引脚区
  //   请勿修改引脚名称、电路名称及电路封装外观
  //   提示：使用16位并行加法器子电路实现32位快速加法器
  //   功能说明:32位Adder  S=X+Y，Cout为最高位进位位，Cin为进位输入， S为和，溢出OF、进位CF、零ZF、符号SF。
  //   +
  //   =
  //   无符号加法
endmodule

// 移位器
module Shifter32 (
  input  [4:0] shamt,
  input  L_R,
  input  A_L,
  input  [31:0] DataIn,
  output [31:0] DataOut
);

  wire multiplexer_9_out, multiplexer_15_out, multiplexer_25_out;
  wire [0:0] multiplexer_2_out;
  wire [3:0] bit_extender_1_out, multiplexer_6_out, multiplexer_13_out;
  wire [7:0] bit_extender_2_out, multiplexer_23_out;
  wire [15:0] bit_extender_3_out, multiplexer_41_out;
  wire [31:0] multiplexer_3_out, multiplexer_8_out, multiplexer_14_out, multiplexer_24_out;
  wire [31:31] multiplexer_1_out;

  Multiplexer #(.enable("false")) multiplexer_1 (.in0(1'b0), .in1(DataIn[31]), .out(multiplexer_1_out[31]), .sel(A_L));
  Multiplexer #(.enable("false")) multiplexer_2 (.in0(1'b0), .in1(DataIn[31]), .out(multiplexer_2_out[0]), .sel(A_L));
  Multiplexer #(.select(2), .width(32), .enable("false")) multiplexer_3 (
    .in0(DataIn), .in1(DataIn), .in2({multiplexer_1_out[31], DataIn[31:1]}),
    .in3({DataIn[30:0], multiplexer_2_out[0]}), .out({multiplexer_3_out[29:0], multiplexer_6_out[3:2]}),
    .sel({shamt[0], L_R}));
  Multiplexer #(.enable("false")) multiplexer_4 (
    .in0(1'b0), .in1(multiplexer_3_out[29]), .out(multiplexer_3_out[31]), .sel(A_L));
  Multiplexer #(.enable("false")) multiplexer_5 (
    .in0(1'b0), .in1(multiplexer_3_out[29]), .out(multiplexer_3_out[30]), .sel(A_L));
  Multiplexer #(.enable("false")) multiplexer_6 (
    .in0(1'b0), .in1(multiplexer_3_out[28]), .out(multiplexer_6_out[0]), .sel(A_L));
  Multiplexer #(.enable("false")) multiplexer_7 (
    .in0(1'b0), .in1(multiplexer_3_out[29]), .out(multiplexer_6_out[1]), .sel(A_L));
  Multiplexer #(.select(2), .width(32), .enable("false")) multiplexer_8 (
    .in0({multiplexer_3_out[29:0], multiplexer_6_out[3:2]}),
    .in1({multiplexer_3_out[29:0], multiplexer_6_out[3:2]}), .in2(multiplexer_3_out),
    .in3({multiplexer_3_out[27:0], multiplexer_6_out}), .out(multiplexer_8_out), .sel({shamt[1], L_R}));
  Multiplexer #(.enable("false")) multiplexer_9 (
    .in0(1'b0), .in1(multiplexer_8_out[31]), .out(multiplexer_9_out), .sel(A_L));
  Multiplexer #(.enable("false")) multiplexer_10 (
    .in0(1'b0), .in1(multiplexer_8_out[31]), .out(multiplexer_13_out[3]), .sel(A_L));
  Multiplexer #(.enable("false")) multiplexer_11 (
    .in0(1'b0), .in1(multiplexer_8_out[30]), .out(multiplexer_13_out[2]), .sel(A_L));
  Multiplexer #(.enable("false")) multiplexer_12 (
    .in0(1'b0), .in1(multiplexer_8_out[29]), .out(multiplexer_13_out[1]), .sel(A_L));
  Multiplexer #(.enable("false")) multiplexer_13 (
    .in0(1'b0), .in1(multiplexer_8_out[28]), .out(multiplexer_13_out[0]), .sel(A_L));
  assign bit_extender_1_out = {{3{multiplexer_9_out}}, multiplexer_9_out};  // Bit_Extender bit_extender_1
  Multiplexer #(.select(2), .width(32), .enable("false")) multiplexer_14 (
    .in0(multiplexer_8_out), .in1(multiplexer_8_out), .in2({bit_extender_1_out, multiplexer_8_out[31:4]}),
    .in3({multiplexer_8_out[27:0], multiplexer_13_out}), .out(multiplexer_14_out), .sel({shamt[2], L_R}));
  Multiplexer #(.enable("false")) multiplexer_15 (
    .in0(1'b0), .in1(multiplexer_14_out[31]), .out(multiplexer_15_out), .sel(A_L));
  Multiplexer #(.enable("false")) multiplexer_16 (
    .in0(1'b0), .in1(multiplexer_14_out[31]), .out(multiplexer_23_out[7]), .sel(A_L));
  Multiplexer #(.enable("false")) multiplexer_17 (
    .in0(1'b0), .in1(multiplexer_14_out[30]), .out(multiplexer_23_out[6]), .sel(A_L));
  Multiplexer #(.enable("false")) multiplexer_18 (
    .in0(1'b0), .in1(multiplexer_14_out[29]), .out(multiplexer_23_out[5]), .sel(A_L));
  Multiplexer #(.enable("false")) multiplexer_19 (
    .in0(1'b0), .in1(multiplexer_14_out[28]), .out(multiplexer_23_out[4]), .sel(A_L));
  Multiplexer #(.enable("false")) multiplexer_20 (
    .in0(1'b0), .in1(multiplexer_14_out[27]), .out(multiplexer_23_out[3]), .sel(A_L));
  Multiplexer #(.enable("false")) multiplexer_21 (
    .in0(1'b0), .in1(multiplexer_14_out[26]), .out(multiplexer_23_out[2]), .sel(A_L));
  Multiplexer #(.enable("false")) multiplexer_22 (
    .in0(1'b0), .in1(multiplexer_14_out[25]), .out(multiplexer_23_out[1]), .sel(A_L));
  Multiplexer #(.enable("false")) multiplexer_23 (
    .in0(1'b0), .in1(multiplexer_14_out[24]), .out(multiplexer_23_out[0]), .sel(A_L));
  assign bit_extender_2_out = {{7{multiplexer_15_out}}, multiplexer_15_out};  // Bit_Extender bit_extender_2
  Multiplexer #(.select(2), .width(32), .enable("false")) multiplexer_24 (
    .in0(multiplexer_14_out), .in1(multiplexer_14_out), .in2({bit_extender_2_out, multiplexer_14_out[31:8]}),
    .in3({multiplexer_14_out[23:0], multiplexer_23_out}), .out(multiplexer_24_out), .sel({shamt[3], L_R}));
  Multiplexer #(.enable("false")) multiplexer_25 (
    .in0(1'b0), .in1(multiplexer_24_out[31]), .out(multiplexer_25_out), .sel(A_L));
  Multiplexer #(.enable("false")) multiplexer_26 (
    .in0(1'b0), .in1(multiplexer_24_out[31]), .out(multiplexer_41_out[15]), .sel(A_L));
  Multiplexer #(.enable("false")) multiplexer_27 (
    .in0(1'b0), .in1(multiplexer_24_out[29]), .out(multiplexer_41_out[13]), .sel(A_L));
  Multiplexer #(.enable("false")) multiplexer_28 (
    .in0(1'b0), .in1(multiplexer_24_out[30]), .out(multiplexer_41_out[14]), .sel(A_L));
  Multiplexer #(.enable("false")) multiplexer_29 (
    .in0(1'b0), .in1(multiplexer_24_out[28]), .out(multiplexer_41_out[12]), .sel(A_L));
  Multiplexer #(.enable("false")) multiplexer_30 (
    .in0(1'b0), .in1(multiplexer_24_out[27]), .out(multiplexer_41_out[11]), .sel(A_L));
  Multiplexer #(.enable("false")) multiplexer_31 (
    .in0(1'b0), .in1(multiplexer_24_out[26]), .out(multiplexer_41_out[10]), .sel(A_L));
  Multiplexer #(.enable("false")) multiplexer_32 (
    .in0(1'b0), .in1(multiplexer_24_out[25]), .out(multiplexer_41_out[9]), .sel(A_L));
  Multiplexer #(.enable("false")) multiplexer_33 (
    .in0(1'b0), .in1(multiplexer_24_out[24]), .out(multiplexer_41_out[8]), .sel(A_L));
  Multiplexer #(.enable("false")) multiplexer_34 (
    .in0(1'b0), .in1(multiplexer_24_out[23]), .out(multiplexer_41_out[7]), .sel(A_L));
  Multiplexer #(.enable("false")) multiplexer_35 (
    .in0(1'b0), .in1(multiplexer_24_out[21]), .out(multiplexer_41_out[5]), .sel(A_L));
  Multiplexer #(.enable("false")) multiplexer_36 (
    .in0(1'b0), .in1(multiplexer_24_out[22]), .out(multiplexer_41_out[6]), .sel(A_L));
  Multiplexer #(.enable("false")) multiplexer_37 (
    .in0(1'b0), .in1(multiplexer_24_out[20]), .out(multiplexer_41_out[4]), .sel(A_L));
  Multiplexer #(.enable("false")) multiplexer_38 (
    .in0(1'b0), .in1(multiplexer_24_out[19]), .out(multiplexer_41_out[3]), .sel(A_L));
  Multiplexer #(.enable("false")) multiplexer_39 (
    .in0(1'b0), .in1(multiplexer_24_out[18]), .out(multiplexer_41_out[2]), .sel(A_L));
  Multiplexer #(.enable("false")) multiplexer_40 (
    .in0(1'b0), .in1(multiplexer_24_out[17]), .out(multiplexer_41_out[1]), .sel(A_L));
  Multiplexer #(.enable("false")) multiplexer_41 (
    .in0(1'b0), .in1(multiplexer_24_out[16]), .out(multiplexer_41_out[0]), .sel(A_L));
  assign bit_extender_3_out = {{15{multiplexer_25_out}}, multiplexer_25_out};  // Bit_Extender bit_extender_3
  Multiplexer #(.select(2), .width(32), .enable("false")) multiplexer_42 (
    .in0(multiplexer_24_out), .in1(multiplexer_24_out),
    .in2({bit_extender_3_out, multiplexer_24_out[31:16]}),
    .in3({multiplexer_24_out[15:0], multiplexer_41_out}), .out(DataOut), .sel({shamt[4], L_R}));

  // Other names for the same wires on the sheet: Din[31:0] = DataIn; Left_Right = L_R; Arth_Logic = A_L;
  //   Dout[31:0] = DataOut

  // Notes on the sheet:
  //   L/R,A/L: 00逻辑右移，01算术右移，10逻辑左移，11：循环左移
  //   输入引脚
  //   请勿修改引脚名称、电路名称及电路封装外观
  //   提示：使用多路选择器、逻辑门实现32位桶形移位器，禁止直接使用移位器组件。
  //   输出引脚
endmodule

module Adder16 (
  input  C0,
  input  [15:0] X,
  input  [15:0] Y,
  output C16,
  output Pg,
  output Gg,
  output [15:0] S
);

  wire cla4_1_gg, cla4_1_pg, cla4_2_gg, cla4_2_pg, cla4_3_gg, cla4_3_pg, cla4_4_gg, cla4_4_pg, clu4_1_c1,
       clu4_1_c2, clu4_1_c3;

  CLA4 cla4_1 (
    .X(X[15:12]), .F(S[15:12]), .Y(Y[15:12]), .Pg(cla4_1_pg), .Cin(clu4_1_c3), .Gg(cla4_1_gg));  // open: Cout
  CLA4 cla4_2 (.X(X[11:8]), .F(S[11:8]), .Y(Y[11:8]), .Pg(cla4_2_pg), .Cin(clu4_1_c2), .Gg(cla4_2_gg));  // open: Cout
  CLU4 clu4_1 (
    .P0(cla4_4_pg), .P1(cla4_3_pg), .P2(cla4_2_pg), .P3(cla4_1_pg), .C1(clu4_1_c1), .C3(clu4_1_c3),
    .G0(cla4_4_gg), .G1(cla4_3_gg), .G2(cla4_2_gg), .G3(cla4_1_gg), .C2(clu4_1_c2), .C4(C16), .C0(C0),
    .Pg(Pg), .Gg(Gg));
  CLA4 cla4_3 (.X(X[7:4]), .F(S[7:4]), .Y(Y[7:4]), .Pg(cla4_3_pg), .Cin(clu4_1_c1), .Gg(cla4_3_gg));  // open: Cout
  CLA4 cla4_4 (.X(X[3:0]), .F(S[3:0]), .Y(Y[3:0]), .Pg(cla4_4_pg), .Cin(C0), .Gg(cla4_4_gg));  // open: Cout
  // Probe on X
  // Probe on Y
  // Probe on S

  // Notes on the sheet:
  //   Y: pull=down
  //   X: pull=down
  //   C0: pull=down
  //   输入引脚区
  //   请勿修改引脚名称、电路名称及电路封装外观
  //   提示：使用4位先行进位加法器和CLU子电路实现16位并行加法器
  //   功能说明:16位Adder  S=X+Y，C16为最高位进位位，C0为进位输入， Pg、Gg为成组进位生成传递函数
  //   输出引脚区
  //   +
  //   =
  //   无符号加法
endmodule

module CLA4 (
  input  [3:0] X,
  input  [3:0] Y,
  input  Cin,
  output [3:0] F,
  output Cout,
  output Pg,
  output Gg
);

  wire clu4_1_c1, clu4_1_c2, clu4_1_c3, fa_1_g, fa_1_p, fa_2_g, fa_2_p, fa_3_g, fa_3_p, fa_4_g, fa_4_p;

  Hex_Digit_Display hex_digit_display_1 (.value(X));  // open: dp
  FA fa_1 (.A(X[3]), .F(F[3]), .B(Y[3]), .P(fa_1_p), .Cin(clu4_1_c3), .G(fa_1_g));
  Hex_Digit_Display hex_digit_display_2 (.value(Y));  // open: dp
  FA fa_2 (.A(X[1]), .F(F[1]), .B(Y[1]), .P(fa_2_p), .Cin(clu4_1_c1), .G(fa_2_g));
  FA fa_3 (.A(X[2]), .F(F[2]), .B(Y[2]), .P(fa_3_p), .Cin(clu4_1_c2), .G(fa_3_g));
  Hex_Digit_Display hex_digit_display_3 (.value(F));  // open: dp
  CLU4 clu4_1 (
    .P0(fa_4_p), .P1(fa_2_p), .P2(fa_3_p), .P3(fa_1_p), .C1(clu4_1_c1), .C3(clu4_1_c3), .G0(fa_4_g),
    .G1(fa_2_g), .G2(fa_3_g), .G3(fa_1_g), .C2(clu4_1_c2), .C4(Cout), .C0(Cin), .Pg(Pg), .Gg(Gg));
  FA fa_4 (.A(X[0]), .F(F[0]), .B(Y[0]), .P(fa_4_p), .Cin(Cin), .G(fa_4_g));

  // Other names for the same wires on the sheet: Z[3:0] = F

  // Notes on the sheet:
  //   +
  //   =
  //   输出
  //   输入
  //   请勿修改引脚名称、电路名称及电路封装外观
  //   提示：使用全加器和CLU子电路实现四位先行进位加法器CLA4
endmodule

module CLU4 (
  input  P0,
  input  P1,
  input  P2,
  input  P3,
  input  G0,
  input  G1,
  input  G2,
  input  G3,
  input  C0,
  output C1,
  output C3,
  output C2,
  output C4,
  output Pg,
  output Gg
);

  wire and_1_out, and_2_out, and_3_out, and_4_out, and_5_out, and_6_out, and_7_out, and_8_out, and_9_out,
       and_10_out, and_11_out, and_12_out, and_13_out;

  and and_1 (and_1_out, C0, P0);
  and and_2 (and_2_out, C0, P0, P1);
  and and_3 (and_3_out, G0, P1);
  and and_4 (and_4_out, C0, P0, P1, P2);
  and and_5 (and_5_out, G0, P1, P2);
  and and_6 (and_6_out, G1, P2);
  and and_7 (and_7_out, C0, P0, P1, P2, P3);
  and and_8 (and_8_out, G0, P1, P2, P3);
  and and_9 (and_9_out, G1, P2, P3);
  and and_10 (and_10_out, G2, P3);
  and and_11 (and_11_out, G0, P1, P2, P3);
  and and_12 (and_12_out, G1, P2, P3);
  and and_13 (and_13_out, G2, P3);
  or or_1 (C1, and_1_out, G0);
  or or_2 (C2, and_2_out, and_3_out, G1);
  or or_3 (C3, and_4_out, and_5_out, and_6_out, G2);
  or or_4 (C4, and_7_out, and_8_out, and_9_out, and_10_out, G3);
  and and_14 (Pg, P0, P1, P2, P3);
  or or_5 (Gg, and_11_out, and_12_out, and_13_out, G3);

  // Notes on the sheet:
  //   输入引脚
  //   请勿修改引脚名称、电路名称及电路封装外观
  //   提示：使用逻辑门电路实现4位四位先行进位部件CLU，Pg、Gg为成组进位生成传递函数
  //   输出引脚
endmodule

module FA (
  input  A,
  input  B,
  input  Cin,
  output F,
  output P,
  output G
);

  wire xor_1_out;

  xor xor_1 (xor_1_out, A, B);
  and and_1 (G, A, B);
  or or_1 (P, A, B);
  xor xor_2 (F, xor_1_out, Cin);

  // Notes on the sheet:
  //   输入引脚
  //   请勿修改引脚名称、电路名称及电路封装外观
  //   输出引脚
endmodule

module SEL (
  input  Mem2,
  input  Mem1,
  input  Mem0,
  input  Addr1,
  input  Addr0,
  output Sel3,
  output Sel2,
  output Sel1,
  output Sel0
);

  wire and_1_out, and_2_out, and_3_out, and_4_out, and_5_out, and_6_out, and_7_out, and_8_out, and_9_out,
       and_10_out, and_11_out, and_12_out, not_1_out, not_2_out, not_3_out, not_4_out, not_5_out, not_6_out,
       not_7_out, not_8_out, not_9_out, not_10_out, not_11_out, not_12_out, not_13_out, not_14_out,
       not_15_out, not_16_out, not_17_out, not_18_out, not_19_out, not_20_out, not_21_out, not_22_out,
       not_23_out, not_24_out, not_25_out, not_26_out, not_27_out, not_28_out, not_29_out, not_30_out,
       not_31_out, not_32_out, not_33_out, not_34_out, not_35_out, not_36_out;

  not not_1 (not_1_out, Mem2);
  not not_2 (not_2_out, Mem1);
  not not_3 (not_3_out, Mem0);
  not not_4 (not_4_out, Addr1);
  not not_5 (not_5_out, Addr0);
  not not_6 (not_6_out, Mem1);
  not not_7 (not_7_out, Mem0);
  not not_8 (not_8_out, Addr0);
  not not_9 (not_9_out, Mem2);
  not not_10 (not_10_out, Mem1);
  not not_11 (not_11_out, Mem0);
  not not_12 (not_12_out, Addr1);
  not not_13 (not_13_out, Addr0);
  not not_14 (not_14_out, Mem1);
  not not_15 (not_15_out, Addr0);
  not not_16 (not_16_out, Mem0);
  not not_17 (not_17_out, Addr0);
  not not_18 (not_18_out, Mem2);
  not not_19 (not_19_out, Mem0);
  not not_20 (not_20_out, Addr1);
  not not_21 (not_21_out, Addr0);
  not not_22 (not_22_out, Mem1);
  not not_23 (not_23_out, Addr1);
  not not_24 (not_24_out, Mem0);
  not not_25 (not_25_out, Addr1);
  not not_26 (not_26_out, Addr0);
  not not_27 (not_27_out, Mem2);
  not not_28 (not_28_out, Mem1);
  not not_29 (not_29_out, Addr1);
  not not_30 (not_30_out, Addr0);
  not not_31 (not_31_out, Mem1);
  not not_32 (not_32_out, Addr1);
  not not_33 (not_33_out, Addr0);
  not not_34 (not_34_out, Mem0);
  not not_35 (not_35_out, Addr1);
  not not_36 (not_36_out, Addr0);
  and and_1 (and_1_out, not_1_out, not_2_out, not_3_out, not_4_out, not_5_out);
  and and_2 (and_2_out, not_6_out, Mem0, Addr1, Addr0);
  and and_3 (and_3_out, Mem1, not_7_out, Addr1, not_8_out);
  and and_4 (and_4_out, not_9_out, not_10_out, not_11_out, not_12_out, not_13_out);
  and and_5 (and_5_out, not_14_out, Mem0, Addr1, not_15_out);
  and and_6 (and_6_out, Mem1, not_16_out, Addr1, not_17_out);
  and and_7 (and_7_out, not_18_out, not_19_out, not_20_out, not_21_out);
  and and_8 (and_8_out, not_22_out, Mem0, not_23_out, Addr0);
  and and_9 (and_9_out, Mem1, not_24_out, not_25_out, not_26_out);
  and and_10 (and_10_out, not_27_out, not_28_out, not_29_out, not_30_out);
  and and_11 (and_11_out, not_31_out, Mem0, not_32_out, not_33_out);
  and and_12 (and_12_out, Mem1, not_34_out, not_35_out, not_36_out);
  or or_1 (Sel3, and_1_out, and_2_out, and_3_out);
  or or_2 (Sel2, and_4_out, and_5_out, and_6_out);
  or or_3 (Sel1, and_7_out, and_8_out, and_9_out);
  or or_4 (Sel0, and_10_out, and_11_out, and_12_out);
endmodule
